// Logisim project LogicFuncTools.circ as structural Verilog: 5 circuits, main circuit 布尔表达式
// Bool
module \布尔表达式  (
  input  A,
  input  B,
  input  C,
  output F
);

  wire and_1_out, and_2_out, and_3_out;

  and and_1 (and_1_out, A, B);
  and and_2 (and_2_out, A, C);
  and and_3 (and_3_out, B, C);
  or or_1 (F, and_1_out, and_2_out, and_3_out);

  // Notes on the sheet:
  //   输入引脚
  //   请勿增加、删除引脚，用隧道标签构建电路
  //   请勿更改电路封装外观
  //   输出引脚
  //   武汉纺织大学数字逻辑课程组
endmodule

// Truth
module \真值表  (
  input  A,
  input  B,
  input  C,
  output F
);

  wire and_1_out, and_2_out, and_3_out;

  and and_1 (and_1_out, B, C);
  and and_2 (and_2_out, A, C);
  and and_3 (and_3_out, A, B);
  or or_1 (F, and_1_out, and_2_out, and_3_out);
endmodule

// sTruth
module \简化真值表  (
  input  X1,
  input  X0,
  input  Y1,
  input  Y0,
  output Gt
);


  // Notes on the sheet:
  //   输入引脚
  //   请勿增加、删除引脚，用隧道标签构建电路
  //   请勿更改电路封装外观
  //   输出引脚
  //   武汉纺织大学数字逻辑课程组
endmodule

// Wave
module \波形图  (
  input  A,
  input  B,
  input  C,
  output F
);


  // Notes on the sheet:
  //   输入引脚
  //   A
  //   B
  //   C
  //   F
  //   请勿增加、删除引脚，用隧道标签构建电路
  //   请勿更改电路封装外观
  //   输出引脚
  //   武汉纺织大学数字逻辑课程组
endmodule

// Kmap
module \卡诺图  (
  input  A,
  input  B,
  input  C,
  input  D,
  output F
);


  // Notes on the sheet:
  //   输入引脚
  //   请勿增加、删除引脚，用隧道标签构建电路
  //   请勿更改电路封装外观
  //   输出引脚
  //   武汉纺织大学数字逻辑课程组
endmodule
