// Logisim project storage.circ as structural Verilog: 18 circuits, main circuit ◇MIPS Regfile
// 字库
module \字库电路  (
  input  [6:0] \区号 ,
  input  [6:0] \位号 ,
  output [31:0] D0,
  output [31:0] D1,
  output [31:0] D6,
  output [31:0] D3,
  output [31:0] D4,
  output [31:0] D5,
  output [31:0] D6_2,
  output [31:0] D7
);

  wire [1:0] subtractor_2_out_2;
  wire [6:0] multiplier_1_cout, multiplier_1_out, subtractor_1_out;
  wire [11:0] subtractor_2_out;
  wire [13:0] adder_1_out, bit_extender_1_out;
  wire [31:0] rom_1_data, rom_4_data, rom_6_data, rom_9_data;

  ROM #(.addrWidth(12), .dataWidth(32), .Select("high")) rom_1 (.addr(subtractor_2_out), .data(rom_1_data));
  ROM #(.addrWidth(14), .dataWidth(32), .Select("high")) rom_2 (
    .addr({subtractor_2_out_2, subtractor_2_out}), .data(D0));
  ROM #(.addrWidth(14), .dataWidth(32), .Select("high")) rom_3 (
    .addr({subtractor_2_out_2, subtractor_2_out}), .data(D4));
  Subtractor #(.width(7)) subtractor_1 (.a(\区号 ), .b(7'b0000001), .out(subtractor_1_out));  // open: bin, bout
  Multiplier #(.width(7)) multiplier_1 (
    .a(subtractor_1_out), .b(7'b1011110), .out(multiplier_1_out), .cout(multiplier_1_cout));  // open: cin
  ROM #(.addrWidth(12), .dataWidth(32), .Select("high")) rom_4 (.addr(subtractor_2_out), .data(rom_4_data));
  ROM #(.addrWidth(14), .dataWidth(32), .Select("high")) rom_5 (
    .addr({subtractor_2_out_2, subtractor_2_out}), .data(D5));
  assign bit_extender_1_out = {{7{1'b0}}, \位号 };  // Bit_Extender bit_extender_1
  Adder #(.width(14)) adder_1 (
    .a({multiplier_1_cout, multiplier_1_out}), .b(bit_extender_1_out), .out(adder_1_out));  // open: cin, cout
  ROM #(.addrWidth(12), .dataWidth(32), .Select("high")) rom_6 (.addr(subtractor_2_out), .data(rom_6_data));
  ROM #(.addrWidth(14), .dataWidth(32), .Select("high")) rom_7 (
    .addr({subtractor_2_out_2, subtractor_2_out}), .data(D6));
  ROM #(.addrWidth(14), .dataWidth(32), .Select("high")) rom_8 (
    .addr({subtractor_2_out_2, subtractor_2_out}), .data(D6_2));
  Subtractor #(.width(14)) subtractor_2 (
    .a(adder_1_out), .b(14'h1), .out({subtractor_2_out_2, subtractor_2_out}));  // open: bin, bout
  DotMatrix #(.inputtype("row"), .matrixcols(16), .matrixrows(16), .persist(0), .dotshape("circle")) dotmatrix_1 (
    .row0(D0[15:0]), .row1(D0[31:16]), .row2(D1[15:0]), .row3(D1[31:16]), .row4(D6[15:0]), .row5(D6[31:16]),
    .row6(D3[15:0]), .row7(D3[31:16]), .row8(D4[15:0]), .row9(D4[31:16]), .row10(D5[15:0]),
    .row11(D5[31:16]), .row12(D6_2[15:0]), .row13(D6_2[31:16]), .row14(D7[15:0]), .row15(D7[31:16]));
  ROM #(.addrWidth(12), .dataWidth(32), .Select("high")) rom_9 (.addr(subtractor_2_out), .data(rom_9_data));
  ROM #(.addrWidth(14), .dataWidth(32), .Select("high")) rom_10 (
    .addr({subtractor_2_out_2, subtractor_2_out}), .data(D3));
  ROM #(.addrWidth(14), .dataWidth(32), .Select("high")) rom_11 (
    .addr({subtractor_2_out_2, subtractor_2_out}), .data(D7));
  Multiplexer #(.select(2), .width(32), .disabled("Z"), .enable("false")) multiplexer_1 (
    .in0(rom_1_data), .in1(rom_4_data), .in2(rom_6_data), .in3(rom_9_data), .out(D1), .sel(subtractor_2_out_2));

  // Other names for the same wires on the sheet: D2[31:0] = D6; D6_t[31:0] = D6_2

  // Notes on the sheet:
  //   输入引脚区
  //   输入引脚区
  //   请勿增改引脚，请勿修改子电路封装
  //   contents of rom_1 (hex, n*v repeats v):
  //   7*0 1100000 3000380 0 0 2400240 0 100008 c000c00 440022 33003300 600038 3000e00 400000 1000200
  //   2400000 2400000 10001f0 800080 20803f8 500070 8200ff0 20807f8 7e007f0 3f007f0 800080 0 0 0 2200140
  //   20020000 18041ffc 18183ffc 10041004 180c0c18 30000c0 18180000 100008 800080 1200120 100008 63001c0
  //   20021004 900060 1000090 0 10480830 0 0 0 200020 230020c 1a00620 1800060 c00300 0 3c3c1818 3c00180
  //   2a001c0 2200220 2200220 600020 1b00090 33e84800 3f00090 163421c2 6b003f0 f80070 24101808 2000220
  //   1c401870 1400140 1c001c0 10080c30 1ff80ff0 263211c4 4100220 7f003e0 20043ffc 3ffc3ffc 14001c0
  //   1c001c0 11880000 0 0 1c001c0 800080 3ffc3ffc 16*0 3000700 cc00780 cc00780 3800180 18001fe0 cc00780
  //   1fe01fe0 cc00780 cc00780 1b1839b0 c601ce0 71e010c0 736011c0 70601020 730013f8 71b010e0 73f813f8
  //   71b010e0 71b010e0 799830f0 13841084 136411c4 136411c4 11c410c4 17f41004 133411e4 17f41004 136411c4
  //   11c41004 2c942464 2c642424 2c942464 2c942464 2c642424 2c8424f4 2c942464 2c9424f4 2c942464 2c942464
  //   29542624 21c21044 236211c4 236211c4 20c21044 27f21004 233211e4 27f21004 236211c4 21c21004 2eda1274 0
  //   0 20042004 20242004 2ff42024 28142004 2ff42024 21142104 21042104 22442044 22042204 20842084 0 0
  //   8001c0 2200770 8881ddc 8881ddc 4100e38 8881ddc 11143bbe 11543bfe 8881ddc 4100e38 8881ddc 11283bfc
  //   c300000 0 3c003c0 4200000 2200220 380c7c1e 12080c04 19000e0 700000 100008 8001000 0 800000 0 0 0
  //   80004 63003e0 3800080 66003c0 66003c0 1c000c0 c000ff0 66003c0 ff00ff0 66003c0 66003c0 0 0 30000c 0
  //   c003000 181807f0 41003e0 1c00080 c381fe0 63803e0 c701fc0 c181ff8 c181ff8 61c03f0 c181e3c 18003c0
  //   c001e0 c301e7c c001e00 180c380e e101c38 63003e0 c301fe0 e3803e0 c301fe0 c1807e8 318c3ffc c081e1c
  //   18083c1c 18c43dee c081e1c 380c7c1e 20183ff8 6000600 18003000 300030 800000 0 800180 0 6000e00 0
  //   6000e0 0 19800f0 0 6000e00 1800000 c00000 6000e00 1800380 7*0 800000 6*0 1000100 800080 400040 0
  //   1000100 1000080 8000000 10001000 7c00000 6007c0 1800300 8003c0 4600800 40c0818 1000200 1000206
  //   1f00200 1f60208 c00040 c60048 10101030 10131024 fc00000 fc60008 1000200 1060208 4000400 410040c
  //   800080 860088 2200020 2260028 24007c0 24607c8 4380400 43b0404 c9000a0 c9300a4 0 0 60008 3c0000
  //   3b0004 1000100 1080106 4300400 8080800 2700400 8600800 c600380 9240820 9230824 9240822 6180010
  //   61b0014 61a0015 3000000 310000c 3140008 0 10000c 140008 8200820 8230824 8220825 800080 f000000
  //   1f000400 13c01080 7000100 3400000 6000000 700020 10ec1050 800080 e00080 6000c0 4000400 64009c0
  //   8600800 64009c0 4000800 4000800 3e000000 8003c0 7c00100 1000100 11*0 ff80000 980004 600000 f8001e0
  //   800080 ffe0040 0 ff80000 200000 100010 1000100 1060108 1000200 1060208 4000200 4060208 4000200
  //   4060200 0 60008 2200220 2260228 6000c00 6060c08 ff80000 ff60008 2000200 2060208 100010 160008
  //   4000200 4060208 f0000f0 f0600e8 0 11080000 110e0008 ff0 60fe8 2000200 2060208 800080 ff80000 ff80000
  //   800100 300010 1000000 1060008 104000a 2000200 2060208 204020a 1ff80000 1ff60008 1ffa0004 0 60008
  //   40008 800080 860088 820085 0 1e00e00 c00040 180008 7f00000 2000000 4000400 0 0 7f00000 41ffc 7f0
  //   4400040 4400440 4000400 ffc0000 0 ffe0000 800080 ff80000 81ff8 c000000 430044 800080 1000000 8*0
  //   14001c0 e381ff0 e181ff8 1c001c0 e181ff8 20183ff8 c181e3c 63003e0 18003c0 c301e78 14001c0 380e0000
  //   e081c1c ff80ff8 63003e0 c181ffc e301fe0 8080ff8 11881ff8 1bc80e6c 18003c0 c081e1c 118823c4 c180630
  //   8*0 7200000 36000c0 80000 67003c0 3c00000 2600120 5b000e0 36001c0 7000100 e100200 a000400 c300000 0
  //   2200180 1c00000 0 33001e0 1f80000 fe00000 0 1000100 a100408 11000100 2200000 38*0 14001c0 e181ff8
  //   e381ff0 e181ff8 2300ff8 e181ff8 1ff80000 399c73ce 18381470 c181e3c 1e3c03e0 c341e18 2300ff8 380e0000
  //   c181e3c 63003e0 c181ffc e301fe0 63803e0 11881ff8 c081e1c 18003c0 c081e1c c181e3c c181e3c 318c7bde
  //   318c7bde 16001f00 18183c3c 6000f00 e300be0 198c3cf8 61803fc 15*0 3800000 38000e0 fe00000 ff00000
  //   ff80000 0 1200000 0 5c00000 f780000 2200000 f100000 ff80000 0 f780000 1c00000 ff80000 6e00000
  //   1e00000 ff00000 f380000 1800380 f380000 f780000 f780000 1ddc0000 1ddc0000 1f000000 1e3c0000 f000000
  //   3c00000 1e7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
  //   contents of rom_2 (hex, n*v repeats v):
  //   8*0 1000000 0 0 2400000 5*0 c0000 18000000 16*0 800000 0 0 0 10040000 7f00000 0 0 80000 800000 0 0 0
  //   c1803e0 0 600000 5*0 200000 0 18200000 180006 c003000 0 0 0 800000 1c00000 1c00000 200000 900000
  //   48003000 0 0 500000 0 40000 1c00000 38300000 800080 800080 3c00000 3c00000 c1803e0 1400080 1c00080 0
  //   0 800000 800000 0 0 0 800000 800000 3ffc0000 16*0 1000000 0 0 800000 5*0 8e00000 4200000 9*0 8080000
  //   8080000 8080000 8480000 5*8080000 11*10080000 10*c1803e0 0 0 5*10080000 11080000 4*10080000 16*0
  //   1800000 6*0 40000 20000000 5*0 20000 4*0 400000 38*0 7f80000 60000000 ff00000 0 0 1000100 26*0
  //   10000c0 800080 400180 0 0 800000 9*0 80000 2000000 2060008 0 60008 200000 30004 0 60008 2000000
  //   2060008 0 100000 800000 860008 0 60008 0 60008 0 30004 800000 830004 0 0 60008 0 30004 0 80000 0 0 0
  //   8000000 0 200000 230004 250002 0 30004 20000 0 100000 0 0 100000 0 f80000 fb0004 fa0000 800000 0
  //   4000000 800000 1000000 0 0 0 200000 0 800000 0 0 0 8000000 5*0 1000000 13*0 1ffe0000 0 3c0000 0
  //   400000 0 0 0 100000 1000000 1060008 2000000 2060008 2000000 2060008 1000000 1060008 0 60008 200000
  //   260008 0 60008 0 60008 0 60008 0 60008 2000000 2060008 0 60008 0 0 60008 0 60008 2000000 2060008 0 0
  //   0 2000000 0 0 60008 40000 0 60008 40000 0 60008 20000 0 60008 40000 0 60008 20000 12*0 400000 400000
  //   4*0 800000 0 0 0 30004 10*0 800000 0 0 800000 6*0 800000 8*0 380000 0 0 0 3e00000 21*0 400000 48*0
  //   800000 5*0 2200000 0 3c00000 0 6300000 38*0 300000 19*0 800000 25*0 800000 4400000 2000000 0 800000
  //   4400000 2000000 0 1000000 4400000 2000000 0 800000 4400000 2000000 0 800000 8800000 2000000 7c00000
  //   1000080 2800440 1000200 0 1000000 0 800000 800000 4400000 2000000 5*0 8000000 4000000 0 0 4000000
  //   1000000 0 1000000 0 0 0 200000 800000 0 1000000 400000 0 0 0 2000000 1000000 10080000 0 1000000 0 0
  //   0 2000000 0 3fe00000 8000000 2000000 0 0 1000000 100000 27*0 1000100 1800180 16*0 1000100 1000100
  //   1800180 1800180 1000100 1000100 1800180 1800180 1000100 1000100 1800180 1000100 1800180 1800180
  //   1000100 1800180 1000100 1000100 1800180 1000100 1800180 1800180 1000100 1800180 8*0 4*1000100
  //   4*1800180 4*1000100 1800180 1000100 1800180 1800180 1800180 1000100 1000100 1800180 1000100 1800180
  //   1800180 1800180 15*0 600000 6*0 80000 10000000 5*0 20000 4*0 200000 38*0 7f80000 60000000 ff00000 0
  //   0 1000100 26*0 400030 800080 1000600 0 600000 6*0 80000 10000000 5*0 20000 4*0 200000 38*0 7f80000
  //   60000000 ff00000 0 0 1000100 26*0 400030 800080 1000600 0 4*300c0ff0 381c0ff0 381c0ff0 300c0ff0
  //   3bdc0ff0 3ffc0ff0 3dfc0ff0 3ffc0ff0 3e7c0ff0 3f7c0ff0 3cfc0ff0 c423c423 2a543bdc 3bdc3bdc d5abc423
  //   294030c 39c030c fd6bfcf3 fce3fdf3 fc3ffe7f 3c00180 3c00180 fc3ffe7f e700420 f18ffbdf 7e00180
  //   f81ffe7f 66003c0 f99ffc3f 7e003c0 f81ffc3f 0 ffffffff 3c00180 1c380000 7e003c0 1800000 381c0ff0
  //   3ffc0ff0 4400000 400000 4000000 1800180 1800180 1800180 c000c0 1800180 1800180 1800180 4*0 1ff80000
  //   8001ffff 0 60002 600060 60004000 6000600 7e0000 700070 7e000000 e000e00 c000c c000c0 0 7000380 0
  //   300c300c 1800000 c000c00 c000c000 30003 0 80008000 10001 0 24001800 10081ff8 1c00000 3800000 4800000
  //   fb7fffff 1000100 38000000 6*0 1c00040 0 1e00060 0 3c001e0 3c000c0 0 0 1b00110 0 7000200 0 3e00120
  //   1e00180 0 0 1800180 0 1800180 0 1800180 1800180 0 0 7e00180 0 1800180 0 7e003c0 5a00180 0 0 3e001e00
  //   0 fc0078 0 1a001e00 ec0078 0 3cb0301 f800e0 0 7d00fe00 40004000 1ff00f0 3ec07580 10000 0 1d781900 0
  //   1800080 0 1df00900 f80098 0 0 2400040 0 2400200 0 4e00200 7700040 0 77fc01f8 12e00c0 0 7000300 0
  //   c8008c0 3c00180 0 1cde0000 1f80078 0 78000800 0 3cc01838 7801c00 0 0 2000200 0 400040 0 2000200
  //   600040 0 0 2000180 0 2000180 0 3000180 0 0 7ff80000 4000000 1000000 1bfe2004 1000000 0 0 1000100 0 0
  //   8000000 0 0 0 10000000 0 800000 0 0 0 800000 7ffc0000 0 1000000 80000 0 ff00020 20*0 7ffc3ffc 7f0000
  //   ff000000 3010301 80c080c0 5*0 ffffffff c000c000 ffffffff 30003 c000c000 30003 ffffffff 0 ffffffff 0
  //   8000ffff 80008000 1ffff 10001 80008000 10001 ffff 112*0 2f7e0004 7ffe0004 10401040 10401040 900090
  //   400040 1040200 10201020 440080 fffe0824 21e02018 4440440 5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
  //   contents of rom_3 (hex, n*v repeats v):
  //   0 0 0 180 0 4100410 c30 4400440 2600030 0 fe61c3 2400240 318c 4*0 400040 1000100 4000800 400020
  //   4800900 1200090 1000100 800080 2800280 500050 8800900 880048 7800700 f00070 800080 1400080 1ff8 0
  //   10040808 4100808 4000200 18181818 10041004 10041004 8000fc0 0 800040 800080 2400240 4000200 20022002
  //   408141c1 1000100 3800540 1ffc0000 3ffc0000 20881104 12042102 12202140 1000080 32006200 380026
  //   21800600 c20030 12242142 1800000 18180000 1c00080 800ff8 0 1000100 4800480 c000c00 9800b0 20022002
  //   19001900 1800180 58c0200 1400220 1352134c 4100808 7f00ff8 20042004 3ffc3ffc 48095005 10042002
  //   1ffc3ffe 20042004 3ffc3ffc 8080808 ff80ff8 2401998 30003c 6001e00 800080 4900080 17*0 3000300
  //   18000c0 6000c0 31801980 600060 18601860 3000300 18600cc0 7e00ce0 1b181b18 c600c60 30c03060 30303060
  //   36603360 30183018 33183318 30403040 331831b0 30f831b8 31981998 21822182 218220c2 20322062 2ff228c2
  //   20322032 26322732 20c22062 26322362 203221f2 44924492 44224422 44424422 44124412 45f24522 44124412
  //   44924492 44224422 44924492 44124412 44524452 40c140c1 418140c1 40314061 4ff144c1 40314031 46314731
  //   40c14061 46314361 40b14371 46d946d9 0 0 40024002 40024002 40024002 4c724a52 42224222 44224462
  //   41024102 44224222 42424242 40824082 0 10080000 800080 2200220 8880888 8500888 3200220 5080508
  //   a140a14 a540a54 8500820 2200140 5080208 a280428 c300c30 0 1800180 0 ff80220 1800180 2180100 cd8058c
  //   0 400040 2000200 1401ffc 800080 0 0 0 2000100 c180c18 1800180 c00060 300060 18c00cc0 300030 c300c30
  //   1800180 c300660 3f00670 30003000 1800 30006000 1ff80000 c0006 8000c0 12341224 7f00430 c0c0c18
  //   18001800 c0c0c0c c000c20 c000c20 183c1800 c180c18 1800180 c000c0 ce00dc0 c000c00 114c134c 8d008d0
  //   180c180c c000fe0 188c180c cc00fe0 180030 1800180 c080c08 6400c20 d680d68 36001c0 1800180 6000300
  //   6000600 6000c0 300030 1004 0 0 7e00060 6180618 c000c00 c600c60 ff00c30 1800180 7800cc0 6300630
  //   1800180 c000c0 7c00660 1800180 18c618c6 c300c30 6300630 6180618 6300630 6000600 1e00300 1800180
  //   c300c30 6200c10 d6808cc 1c00360 3200610 1800060 1000200 0 400020 fe61c3 9b00540 9480550 4000400
  //   8000800 100030 100018 1000080 1000080 c080608 6040504 4440244 4440244 200040 200040 4000c00 4000c00
  //   8100810 8100810 10000000 10000000 200040 200040 4000400 4000400 2800280 2800280 2a00220 2a00220
  //   1c800b80 1c800b80 4000400 4000400 c800b0 c800b0 100008 80008 80008 1000100 1000100 4000300 4000300
  //   4100420 10001000 14040a04 18082c04 12082104 6*10100810 1e00080 1e00080 1e00080 e01180 e01180 e01180
  //   10100810 10100810 10100810 800080 2e201430 16081608 22882104 1c80308 1280604 1240e02 9240924
  //   11221122 400040 400040 2f00200 4200e20 6040388 18202c20 60c0388 c080608 6040504 18040c0c 800140
  //   c019b0 4200620 11*0 2000100 1000180 1000100 800080 200010 100008 800080 800080 2200120 2100110
  //   2080208 2080208 fc000f8 fc000f8 800040 800040 1000080 1000080 80008 80008 2200220 2200220 400020
  //   400020 2200140 2200140 2000200 2000200 400020 400020 800140 800140 1000080 1000080 800040 4*1000080
  //   2000220 2000220 1000080 0 800140 8880490 4000200 10040808 10040808 10040808 2000200 2000200 2000200
  //   1000080 1000080 1000080 201040 201040 201040 10840888 10840888 10840888 2800040 10000000 4100200
  //   1400080 803ffc 800080 1000100 1ff80020 20 100010 40004 400020 4400440 4400440 4400420 8040804 200010
  //   100008 3ffe0880 800080 1000080 400020 100008 1080108 800080 8*0 43007f0 c380c70 c000c00 4300430
  //   c000c20 6000300 c180c18 1a2c1bec 1800180 ce00dc0 4300430 114c134c 8c808c8 41007f0 180c180c c180c18
  //   c000fe0 6000300 1800180 1800180 318c318c 36001c0 18003c0 e301c18 8*0 18c018c0 63006e0 1c00120
  //   c300660 c200600 8000800 6180618 6300630 3000300 66006c0 2200140 c300c30 1200320 2000200 6300630
  //   2400240 d800f60 6300630 3000300 6080608 19303118 2200140 19301110 1d5c194c 38*0 43007f0 c380c70
  //   c380c70 c000c00 8300430 c000c20 c200fe0 db00ff0 380070 d180c98 c980c98 c600cc0 8300430 114c134c
  //   c180c18 180c180c c180c18 c000fe0 18001800 1800180 3600320 318c318c 36001c0 c180c18 3d80678 318c318c
  //   318c318c 6180730 18d81d98 6180730 c000c 1b061b06 31803d8 15*0 c2006e0 6300630 6300660 6000600
  //   8600460 6080c00 40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
  //   输出引脚区
  //   电路功能：利用下图中给定的ROM器件实现汉字16*16点阵字库文件，不允许修改ROM地址数据位宽，字库数据可以通过参考字库导出
  //   contents of rom_4 (hex, n*v repeats v):
  //   280fffe 53fc5048 420fffe 4bfc4950 11001ffe 2007ffc 13f810a0 21242124 45084508 43f838a0 11081108
  //   3e442220 448845fc 48887dfc 20881080 8207efc 57fe7840 11081108 17f830a0 7f241424 20082008 1000100
  //   841080 104817fe 21082108 888f888 104017c0 10441040 4bfe4894 10a010a0 24401820 11083108 48a048a0
  //   44a044a0 547e4444 1df81150 7e7e1444 20002000 49007dc0 14101008 4017fe 840fbc0 200017fc 107ffc
  //   20003ffc 21102f70 48907ff0 104830a0 12041204 28822882 49107bfc 40244004 42043e04 22202210 8203ff8
  //   20a02010 20a02010 49203efe 27fc2048 10001ffe 22201140 11101110 6800880 17fc3040 8200820 1040100
  //   44427ffe 47e44404 27fc1048 111030a0 12203140 3ff82008 1000100 48407c40 20881040 14443444 40844084
  //   11fe1084 14441020 4a884c88 14081090 1441344 13f83208 2040200 fffe0104 52807f4c 10fe1084 104017c0
  //   480848a0 45fe7c00 49fe4400 24200420 25fe0400 257e2494 11180208 108013fe 48447c40 13fe1000 4bfc7c48
  //   11fc1028 17fc3048 11fc1028 8200800 7fe1044 5600300 10400840 20203fe 14500440 2a810a0 10001000 240010
  //   2200200 160213fe 40027ffe 1202fffe 121011f8 4a107df8 7d0221fe 340227fe 40027ffe 220223fe 200fffe
  //   4a024bfe 104037fc 1000100 40100 104017fc 420c4004 27fc1008 784007fc 207cff44 1000fffe 10007ffc
  //   3ffc0090 203ff8 4aa42a90 20881040 fffe0104 20802ffc 12241110 41244104 49fe7c94 11fe1094 4800c80
  //   24fe2444 21fe2094 920fffe 440fffe 1040100 17fe0844 10440940 20082008 27fe2044 7ffc0108 820fffe
  //   4bfc7c48 1ff01110 3ff82108 4a487e48 112411fe 10080840 17fc3444 27fc2444 21082108 20fe3f08 2087ffc
  //   10081ffe 12083208 14041020 fffe0104 40244804 20042040 49fe7d04 1110f0f8 8207ffc 40040804 52487910
  //   12100920 12100920 12081408 14881088 12083208 44427ffe 8907890 1050fe50 48404840 12081208 104037c0
  //   1007ffc 49087dfc 1d0811fc 10201ff0 8001800 401040 3ff82008 2000200 440fffe 10881080 4200400 10101010
  //   11101110 483f48 2007ffc 10881080 11000ff8 92905290 208017fc 120009fc 110811fc 3ffc0090 51127ffe
  //   48887c80 51045100 1ffe1004 18200ff0 10881080 12083208 4403ff8 44444444 110011e0 440fffe 1050fc50
  //   107efe40 49207d38 48407ffc 4a087a08 1df81108 509057fe 10d8f020 10101ff8 6c00100 9201110 48e04ffe
  //   7fc0208 111017fc 120813fc 14d81020 1501248 fe0884 3ff82008 24942790 4807ffc 22203ffc 4fffe 110411fe
  //   3ff80100 1dfc1128 13fc3248 4100400 54444b4c 2407e48 212421fe 4a227bfe 142013fe 5ff84010 51127ffe
  //   fe2223fe 54847c84 55fc1028 17fc0848 11fc2c28 2000200 22003ffe 10101ff0 48407c40 24202710 3c202710
  //   1ff81110 20401040 25fe1e54 102011e0 3ffc0090 48a04910 23c01100 23fe3f04 41044804 1102f70 ffe0804
  //   20a02ffe 10101010 511048a0 1128fd08 ff940918 8200820 4a084bfc 3d0820f8 1007ffc 49027ffe 510848f8
  //   49084508 10401048 11041104 22042200 43b83800 1040100 451028a0 3ef80000 1244327e 8200420 fe4429de
  //   fffc10a0 17fc30a0 ff081108 4bfe7c84 7ffc 1044fc20 8207ffc 17fe1224 17fe0a24 7ffe0804 3ffc1048
  //   3ff80920 1024fea8 51127ffe 9242a04 48507ff8 43ef8 3c2410a8 10483150 41027ffe 11b03040 4f807cfc
  //   1000100 2403fe0 13fe1004 5400920 48487bfc 28a01f7c ff240220 211427fe 274c2440 3f3e2120 15fc1104
  //   29fcfe28 20882080 17fc1048 164013fc 24440444 22481408 48884880 143017a8 88044002 17fe1024 48443f7e
  //   be4c4424 292427a4 12483248 9042402 28882fc8 20803ff8 8061440 820fffe 20001dfc 20403840 8203ff8
  //   407f60 110011e0 c00080 10000ffe 7f541054 3ff82008 4bf84a08 11fc2904 13f81208 11102108 11241104
  //   12241224 1110110c 12441244 20001000 28fc2884 1003ff8 fffe0104 12481240 11241120 10101010 50242010
  //   49fe4900 1ffe1004 14943110 fdfc1088 7f8422e0 10440840 211011f8 7ffc0288 108017fe 4a087ffc 20481c40
  //   1080100 241020 20482040 27fe2080 3ffc0090 51127ffe 3ffe0200 4bfe7c40 20441020 211010a0 124033fc
  //   7ffc0920 28442844 12fc1408 108810fc 20003ffc 200fffe 13fc1108 64842284 11701042 205023f8 204023f8
  //   fe201420 4a027bfe 40027ffe 10101ff0 fe8014fe fffe0104 13fc3248 24443ffe 4ffe7c44 20fe2084 2920fea0
  //   820fffe 201110 7ffe0100 41027ffe 2080100 22202220 fffe0104 24242420 10040ffe 140433fe 100010
  //   49240924 12483124 2104fefe 11103010 11243124 11103010 21103f10 11103010 20802080 11241124 290809fc
  //   928492fe 48907c10 c401030 840fffe 10400040 7e881408 3ff82108 4200223e 12283220 24fe0454 48907c90
  //   4400440 22102010 11f0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
  //   contents of rom_5 (hex, n*v repeats v):
  //   0 18002000 30000000 0 0 2200220 0 8800880 c001c0 0 38 2400240 5*0 400040 1000100 1000200 1000080
  //   2400480 2400120 1000100 800080 2800280 500050 8400880 1080088 7c00780 1f000f0 80 4100220 1800000
  //   1800000 20021004 2200410 8040400 18181818 10041004 10041004 4000800 18180000 3b001080 800080 4800480
  //   1ff80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
  //   图中有一个空白器件，表示少一个器件，请按照字扩展（容量扩展，地址线扩展）的方式利用第一行的存储器完成最终字库，字库文件需要进行简单的分割
  //   contents of rom_6 (hex, n*v repeats v):
  //   18c618c6 4cc03fe 7fcc00ce 7ff800ac 2cff7f8e e1affff 7ffe0cc2 7ffe4862 19987f98 7ffe0186 fffc03ff
  //   7fff0238 3a781830 1bfe1ede ffc0c0c 7fff0332 19ff0982 183018fe ffc0c0c ffc0c0c 198c1d8e d180c18
  //   1b7e13de 14781fff 14701fff 1818181f 359919f9 7f7f7f60 1f8c1fee 189408d8 3d8831fc e6d0c6c 1830194e
  //   7fff0032 6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
  //   contents of rom_7 (hex, n*v repeats v):
  //   5*0 10041004 0 3300110 ffc0608 0 0 2400240 0 300030 10000800 cc00cc 44002200 400040 1000100 1000080
  //   400080 4800240 1200240 1000100 800080 28002f8 500050 8800840 880108 78007c0 f001f0 800080 4100808
  //   1800180 1800180 4100220 10042002 6000c04 18181818 10041004 10041004 4000400 1818 200010 800080
  //   1200120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
  //   contents of rom_8 (hex, n*v repeats v):
  //   0 c000c00 48004800 0 0 1c00140 0 11001100 4000e0 0 0 2400240 5*0 380060 e000300 400080 200 240 240
  //   1000100 f800080 3800280 10101fd0 ff00820 7f80208 7f007e0 7f003f0 ff8 808 180 180 2002 1400220
  //   1ffc1ffc 3c3c1818 c18180c 10041004 3000400 1818 c002e00 1ffc0080 4800480 0 0 c181004 c001200 c001200
  //   5*0 20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
  //   请在下方利用上方输入输出引脚的隧道信号构建电路，ctrl+d复制选择部件
  //   汉字显示验证区
  //   contents of rom_10 (hex, n*v repeats v):
  //   0 0 0 1800000 7f00000 8080808 c300000 6600330 10300c18 7ffe0000 3f800e00 2400240 318c0000 4*0 400040
  //   1000100 4000200 100020 9000480 900120 1000100 800080 2800280 500050 9000880 480088 7000780 7000f0
  //   800ff8 1400220 0 0 8080410 8081004 3000300 18181818 10041004 10041004 8000800 0 400020 800080
  //   2400240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
  //   contents of rom_11 (hex, n*v repeats v):
  //   0 0 3000 0 0 80 5*0 240 5*0 c 1800 7*0 1ff0 9*0 80 0 0 7f0 1004 c0 0 400 4*0 3e0 7*0 200 20c 0 60018
  //   30000c00 10*0 21c2 400 430 0 1c0 605e 2002 2002 0 0 3e0 80 80 7*0 80 80 3ffc 16*0 7b0 8*0 3ce6 1ef6
  //   9*0 9*808 11*1008 10*3e0 0 0 10*1008 23*0 4 2000 17*0 2000 c 0 3000 180 17*0 300048 9*0 7f8 2 ff0 9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
endmodule

module \字库测试  (
);

  wire CLK, comparator_1_eq, d_ff_1_q, not_1_out;
  wire [7:0] counter_1_q;
  wire [15:0] adder_1_out, rom_1_data;
  wire [31:0] R2, R2_S, \参考字库_1_p3 , \参考字库_1_p5 , \参考字库_1_p6 , \参考字库_1_p7 , \参考字库_1_p8 , \参考字库_1_p9 ,
       \参考字库_1_p10 , \字库电路_1_d0 , \字库电路_1_d3 , \字库电路_1_d4 , \字库电路_1_d5 , \字库电路_1_d6 , \字库电路_1_d6_2 ,
       \字库电路_1_d7 ;

  Counter #(.width(8), .max('hff), .ongoal("wrap"), .trigger("rising"), .behavior("old")) counter_1 (
    .Q(counter_1_q), .clk(CLK));  // open: load, D, count, carry, clr, preset
  Clock #(.highDuration(1), .lowDuration(1)) clock_1 (.out(CLK));
  ROM #(.addrWidth(8), .dataWidth(16), .Select("high")) rom_1 (.addr(counter_1_q), .data(rom_1_data));
  Adder #(.width(16)) adder_1 (.a(rom_1_data), .b(16'h5f60), .out(adder_1_out));  // open: cin, cout
  \字库电路  \u_字库电路_1  (
    .D0(\字库电路_1_d0 ), .D1(R2), .D6(\字库电路_1_d6 ), .D3(\字库电路_1_d3 ), .\区号 (adder_1_out[14:8]),
    .\位号 (adder_1_out[6:0]), .D4(\字库电路_1_d4 ), .D5(\字库电路_1_d5 ), .D6_2(\字库电路_1_d6_2 ), .D7(\字库电路_1_d7 ));
  // 参考字库 参考字库_1: pin names not known; wires that end beside it: adder_1_out[14:8], adder_1_out[6:0], \参考字库_1_p3 , R2_S, \参考字库_1_p5 , \参考字库_1_p6 , \参考字库_1_p7 , \参考字库_1_p8 , \参考字库_1_p9 , \参考字库_1_p10 
  Pull_Resistor #(.pull(1)) pull_resistor_1 (.node(R2));
  DotMatrix #(.inputtype("row"), .matrixcols(16), .matrixrows(16), .persist(0), .dotshape("circle")) dotmatrix_1 (
    .row0(\字库电路_1_d0 [15:0]), .row1(\字库电路_1_d0 [31:16]), .row2(R2[15:0]), .row3(R2[31:16]),
    .row4(\字库电路_1_d6 [15:0]), .row5(\字库电路_1_d6 [31:16]), .row6(\字库电路_1_d3 [15:0]), .row7(\字库电路_1_d3 [31:16]),
    .row8(\字库电路_1_d4 [15:0]), .row9(\字库电路_1_d4 [31:16]), .row10(\字库电路_1_d5 [15:0]),
    .row11(\字库电路_1_d5 [31:16]), .row12(\字库电路_1_d6_2 [15:0]), .row13(\字库电路_1_d6_2 [31:16]),
    .row14(\字库电路_1_d7 [15:0]), .row15(\字库电路_1_d7 [31:16]));
  DotMatrix #(.inputtype("row"), .matrixcols(16), .matrixrows(16), .persist(0), .dotshape("circle")) dotmatrix_2 (
    .row0(\参考字库_1_p3 [15:0]), .row1(\参考字库_1_p3 [31:16]), .row2(R2_S[15:0]), .row3(R2_S[31:16]),
    .row4(\参考字库_1_p5 [15:0]), .row5(\参考字库_1_p5 [31:16]), .row6(\参考字库_1_p6 [15:0]), .row7(\参考字库_1_p6 [31:16]),
    .row8(\参考字库_1_p7 [15:0]), .row9(\参考字库_1_p7 [31:16]), .row10(\参考字库_1_p8 [15:0]),
    .row11(\参考字库_1_p8 [31:16]), .row12(\参考字库_1_p9 [15:0]), .row13(\参考字库_1_p9 [31:16]),
    .row14(\参考字库_1_p10 [15:0]), .row15(\参考字库_1_p10 [31:16]));
  Comparator #(.width(32), .mode("twosComplement")) comparator_1 (
    .a(R2_S), .b(R2), .eq(comparator_1_eq));  // open: gt, lt
  not not_1 (not_1_out, comparator_1_eq);
  LED #(.active("true")) led_1 (.in(d_ff_1_q));
  D_Flip_Flop #(.trigger("high"), .Pre_Clr_Positions("LEGACY"), .NegatePresetClear("false"), .enable("true"), .NewFFLayout("false")) d_ff_1 (
    .clk(CLK), .D(not_1_out), .Q(d_ff_1_q));  // open: Qn, preset, en, reset

  // Notes on the sheet:
  //   GB2312
  //   contents of rom_1 (hex, n*v repeats v):
  //   bbaa d6d0 bfc6 bcbc b4f3 d1a7 cac7 b9fa bcd2 bdcc d3fd b2bf d6b1 caf4 b5c4 c8ab b9fa d6d8 b5e3 b4f3
  //   d1a7 a3ac d3c9 d4ad bbaa d6d0 c0ed b9a4 b4f3 d1a7 a1a2 cdac bcc3 d2bd bfc6 b4f3 d1a7 a1a2 cee4 baba
  //   b3c7 cad0 bda8 c9e8 d1a7 d4ba d3da a3b2 a3b0 a3b0 a3b0 c4ea a3b5 d4c2 a3b2 a3b6 c8d5 bacf b2a2 b3c9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
  //   电路功能：字库实现正确性检测，通过对比标准库与待测字库的显示检验功能正确性，ctrl+K驱动电路进行自动仿真
  //   标准库
  //   红灯亮表示有故障
endmodule

module MIPS_RAM (
  input  [11:0] \字节地址 ,
  input  [31:0] Din,
  input  CLK,
  input  WE,
  input  [1:0] Mode,
  output [31:0] DataOut
);

  wire and_1_out, and_2_out, and_3_out, and_4_out, decoder_1_out0, decoder_1_out1, decoder_1_out2,
       decoder_1_out3, decoder_2_out0, decoder_2_out1, multiplexer_2_out, multiplexer_6_out,
       multiplexer_10_out, multiplexer_14_out;
  wire [7:0] _0_data, _1_data, _2_data, _3_data, multiplexer_3_out, multiplexer_4_out, multiplexer_7_out,
       multiplexer_9_out, multiplexer_11_out, multiplexer_12_out, multiplexer_15_out, \计数器_q ;

  Decoder #(.select(2), .tristate("false"), .disabled("Z"), .enable("false")) decoder_1 (
    .out0(decoder_1_out0), .out1(decoder_1_out1), .out2(decoder_1_out2), .out3(decoder_1_out3),
    .sel(\字节地址 [1:0]));
  Multiplexer #(.select(2), .width(8), .disabled("Z"), .enable("false")) multiplexer_1 (
    .in0(_3_data), .in1({8{1'b0}}), .in2({8{1'b0}}), .out(DataOut[31:24]), .sel(Mode));  // open: in3
  and and_1 (and_1_out, WE, multiplexer_2_out);
  Multiplexer #(.select(2), .width(1), .disabled("Z"), .enable("false")) multiplexer_2 (
    .in0(1'b1), .in1(decoder_1_out3), .in2(decoder_2_out1), .out(multiplexer_2_out), .sel(Mode));  // open: in3
  Decoder #(.select(1), .tristate("false"), .disabled("Z"), .enable("false")) decoder_2 (
    .out0(decoder_2_out0), .out1(decoder_2_out1), .sel(\字节地址 [1]));
  Multiplexer #(.select(2), .width(8), .disabled("Z"), .enable("false")) multiplexer_3 (
    .in0(Din[31:24]), .in1(Din[7:0]), .in2(Din[15:8]), .out(multiplexer_3_out), .sel(Mode));  // open: in3
  RAM #(.addrWidth(10), .dataWidth(8), .bus("separate"), .Select("high")) _3 (
    .addr(\字节地址 [11:2]), .din(multiplexer_3_out), .data(_3_data), .str(and_1_out), .clk(CLK));  // open: sel, ld, clr
  Multiplexer #(.select(2), .width(8), .disabled("Z"), .enable("false")) multiplexer_4 (
    .in0(Din[23:16]), .in1(Din[7:0]), .in2(Din[7:0]), .out(multiplexer_4_out), .sel(Mode));  // open: in3
  Multiplexer #(.select(2), .width(8), .disabled("Z"), .enable("false")) multiplexer_5 (
    .in0(_2_data), .in1({8{1'b0}}), .in2({8{1'b0}}), .out(DataOut[23:16]), .sel(Mode));  // open: in3
  and and_2 (and_2_out, WE, multiplexer_6_out);
  Multiplexer #(.select(2), .width(1), .disabled("Z"), .enable("false")) multiplexer_6 (
    .in0(1'b1), .in1(decoder_1_out2), .in2(decoder_2_out1), .out(multiplexer_6_out), .sel(Mode));  // open: in3
  // Probe on DataOut
  RAM #(.addrWidth(10), .dataWidth(8), .bus("separate"), .Select("high")) _2 (
    .addr(\字节地址 [11:2]), .din(multiplexer_4_out), .data(_2_data), .str(and_2_out), .clk(CLK));  // open: sel, ld, clr
  Multiplexer #(.select(2), .width(8), .disabled("Z"), .enable("false")) multiplexer_7 (
    .in0(Din[15:8]), .in1(Din[7:0]), .in2(Din[15:8]), .out(multiplexer_7_out), .sel(Mode));  // open: in3
  Multiplexer #(.select(2), .width(8), .disabled("Z"), .enable("false")) multiplexer_8 (
    .in0(_1_data), .in1({8{1'b0}}), .in2(multiplexer_9_out), .out(DataOut[15:8]), .sel(Mode));  // open: in3
  Multiplexer #(.select(1), .width(8), .disabled("Z"), .enable("false")) multiplexer_9 (
    .in0(_1_data), .in1(_3_data), .out(multiplexer_9_out), .sel(\字节地址 [1]));
  and and_3 (and_3_out, WE, multiplexer_10_out);
  Multiplexer #(.select(2), .width(1), .disabled("Z"), .enable("false")) multiplexer_10 (
    .in0(1'b1), .in1(decoder_1_out1), .in2(decoder_2_out0), .out(multiplexer_10_out), .sel(Mode));  // open: in3
  Counter #(.width(8), .max('hff), .ongoal("wrap"), .trigger("rising"), .behavior("old")) \u_计数器  (
    .Q(\计数器_q ), .clk(CLK));  // open: load, D, count, carry, clr, preset
  // Probe on \计数器_q 
  RAM #(.addrWidth(10), .dataWidth(8), .bus("separate"), .Select("high")) _1 (
    .addr(\字节地址 [11:2]), .din(multiplexer_7_out), .data(_1_data), .str(and_3_out), .clk(CLK));  // open: sel, ld, clr
  Multiplexer #(.select(2), .width(8), .disabled("Z"), .enable("false")) multiplexer_11 (
    .in0(_0_data), .in1(_1_data), .in2(_2_data), .in3(_3_data), .out(multiplexer_11_out), .sel(\字节地址 [1:0]));
  Multiplexer #(.select(2), .width(8), .disabled("Z"), .enable("false")) multiplexer_12 (
    .in0(Din[7:0]), .in1(Din[7:0]), .in2(Din[7:0]), .out(multiplexer_12_out), .sel(Mode));  // open: in3
  Multiplexer #(.select(2), .width(8), .disabled("Z"), .enable("false")) multiplexer_13 (
    .in0(_0_data), .in1(multiplexer_11_out), .in2(multiplexer_15_out), .out(DataOut[7:0]), .sel(Mode));  // open: in3
  and and_4 (and_4_out, WE, multiplexer_14_out);
  Multiplexer #(.select(2), .width(1), .disabled("Z"), .enable("false")) multiplexer_14 (
    .in0(1'b1), .in1(decoder_1_out0), .in2(decoder_2_out0), .out(multiplexer_14_out), .sel(Mode));  // open: in3
  Multiplexer #(.select(1), .width(8), .disabled("Z"), .enable("false")) multiplexer_15 (
    .in0(_0_data), .in1(_2_data), .out(multiplexer_15_out), .sel(\字节地址 [1]));
  RAM #(.addrWidth(10), .dataWidth(8), .bus("separate"), .Select("high")) _0 (
    .addr(\字节地址 [11:2]), .din(multiplexer_12_out), .data(_0_data), .str(and_4_out), .clk(CLK));  // open: sel, ld, clr

  // Other names for the same wires on the sheet: Dout[31:0] = DataOut; Low2[1:0] = \字节地址 [1:0]; Low1 = \字节地址 [1]

  // Notes on the sheet:
  //   输入引脚区
  //   请勿增改引脚，请勿修改子电路封装
  //   电路功能：利用下图中给定的RAM器件实现既既可以按照字节，也可以按照半字，也可以按照32位字访问的MIPS存储器
  //   请在下方利用上方输入输出引脚的隧道信号构建电路，ctrl+d复制选择部件
  //   输出引脚区
  //   为方便测试，注意Dout应一直输出数据，所有数据位不得悬空，所有RAM芯片ld控制端悬空即可
endmodule

module \MIPS_RAM测试  (
);

  wire clock_1_out, comparator_1_eq, comparator_2_eq, comparator_3_eq, err, not_1_out, not_3_out, or_1_out,
       rom_3_data, Testing, \分频器_q ;
  wire [1:0] rom_4_data, rom_5_data;
  wire [7:0] counter_1_q;
  wire [8:0] counter_2_q;
  wire [11:0] rom_1_data;
  wire [15:0] multiplexer_1_out, multiplexer_1_out_2;
  wire [31:0] adder_1_out, Din, Dout, \Dout上拉 , \Dout期望值 , \校验和_q ;

  Clock #(.highDuration(1), .lowDuration(1)) clock_1 (.out(clock_1_out));
  Counter #(.width(8), .max('hff), .ongoal("wrap"), .trigger("rising"), .behavior("old")) counter_1 (
    .count(Testing), .Q(counter_1_q), .clk(not_1_out));  // open: load, D, carry, clr, preset
  not not_1 (not_1_out, \分频器_q );
  Counter #(.width(1), .max('h1), .ongoal("wrap"), .trigger("rising"), .behavior("old")) \u_分频器  (
    .count(Testing), .Q(\分频器_q ), .clk(clock_1_out));  // open: load, D, carry, clr, preset
  Counter #(.width(9), .max('h1ff), .ongoal("wrap"), .trigger("rising"), .behavior("old")) counter_2 (
    .count(Testing), .Q(counter_2_q), .clk(clock_1_out));  // open: load, D, carry, clr, preset
  // Probe on counter_1_q
  // Probe on rom_1_data
  ROM #(.addrWidth(8), .dataWidth(12), .Select("high")) rom_1 (.addr(counter_1_q), .data(rom_1_data));
  ROM #(.addrWidth(8), .dataWidth(32), .Select("high")) rom_2 (.addr(counter_1_q), .data(Din));
  // Probe on Din
  ROM #(.addrWidth(8), .dataWidth(1), .Select("high")) rom_3 (.addr(counter_1_q), .data(rom_3_data));
  // Probe on rom_4_data
  ROM #(.addrWidth(8), .dataWidth(2), .Select("high")) rom_4 (.addr(counter_1_q), .data(rom_4_data));
  ROM #(.addrWidth(8), .dataWidth(2), .Select("high")) rom_5 (.addr(counter_1_q), .data(rom_5_data));
  ROM #(.addrWidth(9), .dataWidth(32), .Select("high")) rom_6 (.addr(counter_2_q), .data(\Dout期望值 ));
  Comparator #(.width(2), .mode("twosComplement")) comparator_1 (
    .a(rom_5_data), .b(2'b11), .eq(comparator_1_eq));  // open: gt, lt
  Comparator #(.width(32), .mode("twosComplement")) comparator_2 (
    .a(\Dout上拉 ), .b(\Dout期望值 ), .eq(comparator_2_eq));  // open: gt, lt
  MIPS_RAM mips_ram_1 (
    .\字节地址 (rom_1_data), .Din(Din), .DataOut(Dout), .CLK(\分频器_q ), .WE(rom_3_data), .Mode(rom_4_data));
  // Probe on Dout
  _7_Segment_Display #(.active("true")) u_7_segment_display_1 (
    .g(multiplexer_1_out[15]), .f(multiplexer_1_out[14]), .a(multiplexer_1_out[13]),
    .b(multiplexer_1_out[12]), .e(multiplexer_1_out_2[15]), .d(multiplexer_1_out_2[14]),
    .c(multiplexer_1_out_2[13]), .dp(multiplexer_1_out_2[12]));
  not not_2 (err, comparator_2_eq);
  and and_1 (Testing, ~comparator_1_eq, comparator_2_eq);  // AND_Gate
  assign \Dout上拉  = Dout;  // Buffer buffer_1, 32 bits wide
  Pull_Resistor #(.pull(1)) pull_resistor_1 (.node(\Dout上拉 ));
  // Probe on \Dout上拉 
  _7_Segment_Display #(.active("true")) u_7_segment_display_2 (
    .g(multiplexer_1_out[7]), .f(multiplexer_1_out[6]), .a(multiplexer_1_out[5]), .b(multiplexer_1_out[4]),
    .e(multiplexer_1_out_2[7]), .d(multiplexer_1_out_2[6]), .c(multiplexer_1_out_2[5]),
    .dp(multiplexer_1_out_2[4]));
  _7_Segment_Display #(.active("true")) u_7_segment_display_3 (
    .g(multiplexer_1_out[11]), .f(multiplexer_1_out[10]), .a(multiplexer_1_out[9]), .b(multiplexer_1_out[8]),
    .e(multiplexer_1_out_2[11]), .d(multiplexer_1_out_2[10]), .c(multiplexer_1_out_2[9]),
    .dp(multiplexer_1_out_2[8]));
  Adder #(.width(32)) adder_1 (.a(\校验和_q ), .b(\Dout上拉 ), .out(adder_1_out));  // open: cin, cout
  _7_Segment_Display #(.active("true")) u_7_segment_display_4 (
    .g(multiplexer_1_out[3]), .f(multiplexer_1_out[2]), .a(multiplexer_1_out[1]), .b(multiplexer_1_out[0]),
    .e(multiplexer_1_out_2[3]), .d(multiplexer_1_out_2[2]), .c(multiplexer_1_out_2[1]),
    .dp(multiplexer_1_out_2[0]));
  // Probe on Din
  Register #(.width(32), .trigger("rising"), .Select("low")) \u_校验和  (
    .D(adder_1_out), .en(not_3_out), .Q(\校验和_q ), .clk(\分频器_q ));  // open: clr
  not not_3 (not_3_out, comparator_1_eq);
  // Probe on Dout
  Multiplexer #(.select(1), .width(32), .disabled(0), .enable("true")) multiplexer_1 (
    .in0(32'h8a8cef44), .in1(32'h8a66ffee), .out({multiplexer_1_out_2, multiplexer_1_out}),
    .sel(comparator_3_eq), .en(or_1_out));
  or or_1 (or_1_out, err, comparator_1_eq);
  // Probe on \Dout上拉 
  Comparator #(.width(32), .mode("twosComplement")) comparator_3 (
    .a(\校验和_q ), .b(32'he1f5edf0), .eq(comparator_3_eq));  // open: gt, lt
  // Probe on \Dout期望值 

  // Notes on the sheet:
  //   测试用例存储器
  //   contents of rom_1 (hex, n*v repeats v):
  //   0 4 8 c 10 14 18 1c 20 24 28 2c 30 34 38 3c 2 6 a e 31 35 39 3d 13 17 1b 1f 12 16 1a 1e 11 15 19 1d
  //   10 14 18 1c 0 4 8 c 10 14 18 1c 20 24 28 2c 30 34 38 3c 0 2 4 6 8 a c e 10 12 14 16 18 1a 1c 1e 20
  //   22 24 26 28 2a 2c 2e 30 32 34 36 38 3a 3c 3e 0 1 2 3 4 5 6 7 8 9 a b c d e f 10 11 12 13 14 15 16 17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
  //   contents of rom_2 (hex, n*v repeats v):
  //   203 607 a0b e0f 4*0 20212223 24252627 28292a2b 2c2d2e2f 30310000 34350000 38390000 3c3d0000 1 405
  //   809 c0d 3233 3637 3a3b 3e3f 10 14 18 1c 11 15 19 1d 12 16 1a 1e 13 17 1b 1f
  //   contents of rom_3 (hex, n*v repeats v):
  //   40*1
  //   contents of rom_4 (hex, n*v repeats v):
  //   16*0 8*2 16*1 16*0 32*2 65*1
  //   用于停机
  //   contents of rom_5 (hex, n*v repeats v):
  //   16*0 8*2 16*1 16*0 32*2 64*1 3
  //   contents of rom_6 (hex, n*v repeats v):
  //   0 203 0 607 0 a0b 0 e0f 9*0 20212223 0 24252627 0 28292a2b 0 2c2d2e2f 0 30310000 0 34350000 0
  //   38390000 0 3c3d0000 0 1 0 405 0 809 0 c0d 0 3233 0 3637 0 3a3b 0 3e3f 0 10 0 14 0 18 0 1c 0 11 0 15
  //   0 19 0 1d 0 12 0 16 0 1a 0 1e 0 13 0 17 0 1b 0 1f 10203 10203 4050607 4050607 8090a0b 8090a0b
  //   c0d0e0f c0d0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
  //   电路功能：测试MIPS RAM存储器， ctrl+k启动时钟后，会自动对完成的MIPS RAM存储器进行批量读写测试，并将最终写入的数据逐一读出进行校验和计算
  //   电路状态稳定后测试正确显示PASS，错误显示FAIL，并且测试系统会停止在出错的时刻，记录测试用例编号，方便故障重现
  //   写入测试时，会将写入前RAM数据和写入后的RAM数据分别和期望值进行比较，如果不等表示数据错误。读出时数据应该和期望一致，否则表示出错。
  //   出错时，系统自动停机，观察上面三个值看看哪里不一样
  //   重新复位，自动运行时钟到出错用例附近单步，观察问题
  //   在错误用例前一拍观察Din数据，再观察写入数据前后读出的数据
endmodule

module MIPS_Regfile (
  input  [4:0] R1_num,
  input  [4:0] R2_num,
  input  [31:0] Din,
  input  [4:0] Write_Reg_num,
  input  Write_Enable,
  input  Clock,
  output [31:0] Reg1Out,
  output [31:0] Reg2Out
);

  wire demultiplexer_1_out1, demultiplexer_1_out2, demultiplexer_1_out3;
  wire [31:0] register_1_q, register_2_q, register_3_q;

  Demultiplexer #(.select(2), .width(1), .tristate("false"), .disabled("Z"), .enable("false")) demultiplexer_1 (
    .out1(demultiplexer_1_out1), .out2(demultiplexer_1_out2), .out3(demultiplexer_1_out3), .in(Write_Enable),
    .sel(Write_Reg_num[1:0]));  // open: out0
  Register #(.width(32), .trigger("rising"), .Select("low")) register_1 (
    .D(Din), .en(demultiplexer_1_out1), .Q(register_1_q), .clk(Clock));  // open: clr
  Register #(.width(32), .trigger("rising"), .Select("low")) register_2 (
    .D(Din), .en(demultiplexer_1_out2), .Q(register_2_q), .clk(Clock));  // open: clr
  Register #(.width(32), .trigger("rising"), .Select("low")) register_3 (
    .D(Din), .en(demultiplexer_1_out3), .Q(register_3_q), .clk(Clock));  // open: clr
  Multiplexer #(.select(2), .width(32), .disabled("Z"), .enable("false")) multiplexer_1 (
    .in0({32{1'b0}}), .in1(register_1_q), .in2(register_2_q), .in3(register_3_q), .out(Reg1Out),
    .sel(R1_num[1:0]));
  Multiplexer #(.select(2), .width(32), .disabled("Z"), .enable("false")) multiplexer_2 (
    .in0({32{1'b0}}), .in1(register_1_q), .in2(register_2_q), .in3(register_3_q), .out(Reg2Out),
    .sel(R2_num[1:0]));

  // Other names for the same wires on the sheet: CLK = Clock; R1_num_t[1:0] = R1_num[1:0];
  //   R2_num_t[1:0] = R2_num[1:0]; RD1[31:0] = Reg1Out; RD2[31:0] = Reg2Out; WE = Write_Enable;
  //   W_num[1:0] = Write_Reg_num[1:0]

  // Notes on the sheet:
  //   输入引脚
  //   电路功能：实现MIPS寄存器组，为简化工作量，寄存器编号高3位不要，最终电路中只需要实现0-3号寄存器，注意0号寄存器恒零
  //   输出引脚
  //   请仔细测试电路，核对功能无误后提交教师进行自动检测评分
endmodule

module \MIPS_Regfile测试  (
);

  wire and_1_out, CLK, comparator_1_eq, comparator_2_eq, comparator_3_eq, comparator_4_eq, Equal, NEQ, nHalt,
       not_1_out, priority_encoder_1_gs, priority_encoder_2_gs, R1_NEQ, R2_NEQ;
  wire [3:0] _1, _2, _3;
  wire [9:0] counter_1_q, counter_2_q;
  wire [15:0] ErrorTrace, otherinput;
  wire [31:0] R1_Ref, R2_Ref, Reg1, Reg2, \regfile评分逻辑_1_total , \regfile评分逻辑_1_正确条数 , WriteData;

  Clock #(.highDuration(1), .lowDuration(1)) clock_1 (.out(CLK));
  Counter #(.width(10), .max('h3ff), .ongoal("wrap"), .trigger("rising"), .behavior("old")) counter_1 (
    .count(nHalt), .Q(counter_1_q), .clk(CLK));  // open: load, D, carry, clr, preset
  LED #(.active("false")) \u_测试完成  (.in(nHalt));
  Counter #(.width(10), .max('h3ff), .ongoal("wrap"), .trigger("rising"), .behavior("old")) counter_2 (
    .count(NEQ), .Q(counter_2_q), .clk(CLK), .clr(not_1_out));  // open: load, D, carry, preset
  not not_1 (not_1_out, nHalt);
  Comparator #(.width(32), .mode("twosComplement")) comparator_1 (
    .a(R1_Ref), .b(Reg1), .eq(comparator_1_eq));  // open: gt, lt
  Comparator #(.width(32), .mode("twosComplement")) comparator_2 (
    .a(R2_Ref), .b(Reg2), .eq(comparator_2_eq));  // open: gt, lt
  Multiplexer #(.select(1), .width(8), .disabled("Z"), .enable("false")) multiplexer_1 (
    .in0({8{1'b1}}), .in1({3'b000, otherinput[9:5]}), .out(ErrorTrace[7:0]), .sel(R2_NEQ));
  Multiplexer #(.select(1), .width(8), .disabled("Z"), .enable("false")) multiplexer_2 (
    .in0({8{1'b1}}), .in1({3'b000, otherinput[4:0]}), .out(ErrorTrace[15:8]), .sel(R1_NEQ));
  ROM #(.addrWidth(10), .dataWidth(32), .Select("high")) rom_1 (.addr(counter_1_q), .data(WriteData));
  ROM #(.addrWidth(10), .dataWidth(16), .Select("high")) rom_2 (.addr(counter_1_q), .data(otherinput));
  ROM #(.addrWidth(10), .dataWidth(32), .Select("high")) rom_3 (.addr(counter_1_q), .data(R1_Ref));
  and and_1 (and_1_out, nHalt, NEQ);
  Priority_Encoder #(.select(1), .disabled("Z")) priority_encoder_1 (
    .in0(comparator_1_eq), .in1(comparator_1_eq), .gs(priority_encoder_1_gs));  // open: out, en_out, en_in
  Priority_Encoder #(.select(1), .disabled("Z")) priority_encoder_2 (
    .in0(comparator_2_eq), .in1(comparator_2_eq), .gs(priority_encoder_2_gs));  // open: out, en_out, en_in
  RAM #(.addrWidth(10), .dataWidth(16), .bus("separate"), .Select("high")) ram_1 (
    .addr(counter_2_q), .din(ErrorTrace), .str(and_1_out), .clk(CLK));  // open: data, sel, ld, clr
  not not_2 (R1_NEQ, priority_encoder_1_gs);
  and and_2 (Equal, priority_encoder_1_gs, priority_encoder_2_gs);
  not not_3 (NEQ, Equal);
  not not_4 (R2_NEQ, priority_encoder_2_gs);
  Hex_Digit_Display hex_digit_display_1 (.value(_3));  // open: dp
  MIPS_Regfile mips_regfile_1 (
    .R1_num(otherinput[4:0]), .R2_num(otherinput[9:5]), .Write_Reg_num(otherinput[14:10]), .Din(WriteData),
    .Write_Enable(otherinput[15]), .Clock(CLK), .Reg1Out(Reg1), .Reg2Out(Reg2));
  // Probe on otherinput[4:0]
  // Probe on otherinput[9:5]
  ROM #(.addrWidth(10), .dataWidth(32), .Select("high")) rom_4 (.addr(counter_1_q), .data(R2_Ref));
  Hex_Digit_Display hex_digit_display_2 (.value(_1));  // open: dp
  Hex_Digit_Display hex_digit_display_3 (.value(_2));  // open: dp
  Comparator #(.width(32), .mode("twosComplement")) comparator_3 (
    .a(WriteData), .b({32{1'b0}}), .eq(comparator_3_eq));  // open: gt, lt
  Comparator #(.width(16), .mode("twosComplement")) comparator_4 (
    .a(otherinput), .b({16{1'b0}}), .eq(comparator_4_eq));  // open: gt, lt
  \Regfile评分逻辑  \regfile评分逻辑_1  (
    .EQ(Equal), .EN(nHalt), .CLK(CLK), .\正确条数 (\regfile评分逻辑_1_正确条数 ), .High(_3), .Low(_1), .Mid(_2),
    .Total(\regfile评分逻辑_1_total ));  // open: Right
  // Probe on \regfile评分逻辑_1_total 
  nand nand_1 (nHalt, comparator_3_eq, comparator_4_eq);
  // Probe on \regfile评分逻辑_1_正确条数 

  // Other names for the same wires on the sheet: r1_num[4:0] = otherinput[4:0]; r2_num[4:0] = otherinput[9:5];
  //   w_num[4:0] = otherinput[14:10]

  // Notes on the sheet:
  //   测试逻辑伪代码：for(i=0;i<N;i++)   
  //   {
  //   }
  //   Write Trace
  //   WE W# R2# R1# Trace
  //   R1 Trace
  //   写寄存器，使reg[i]=i+1; 
  //   容错处理
  //   contents of rom_1 (hex, n*v repeats v):
  //   1 41b8 1bfe 2 44a8 1ca7 3 5f7a 2f2a 4 3d39 6009
  //   contents of rom_2 (hex, n*v repeats v):
  //   8041 c20 462 8441 820 62 8841 20 c62 8c41 820 462
  //   contents of rom_3 (hex, n*v repeats v):
  //   6*0 2 0 3 2 0 3
  //   错误记录R1#R2#
  //   R2 Trace
  //   每次读两个寄存器遍历所有寄存器与标准值比较，如发生异常记录错误寄存器编号；
  //   如果修改过引脚封装外观，可能需要手工连线调整
  //   contents of rom_4 (hex, n*v repeats v):
  //   4*0 2 0 0 2 0 3 2 4
  //   华中科技大学：计算机组成课程组
  //   成绩
  //   trace全零停止
endmodule

module \Cache_直接相联  (
  input  [31:0] BlockDataIn,
  input  [15:0] Addr,
  input  BlkDataReady,
  input  CLK,
  output Miss,
  output [7:0] DataOut
);

  wire and_2_out, and_3_out, and_4_out, and_5_out, and_6_out, and_7_out, and_8_out, and_9_out,
       comparator_1_eq, Hit, L0, L1, L2, L3, L4, L5, L6, L7, register_1_q, register_2_q, register_3_q,
       register_4_q, register_5_q, register_6_q, register_7_q, register_8_q, Valid;
  wire [10:0] register_9_q, register_10_q, register_11_q, register_12_q, register_13_q, register_14_q,
       register_15_q, register_16_q, TagData;
  wire [31:0] register_17_q, register_18_q, register_19_q, register_20_q, register_21_q, register_22_q,
       register_23_q, register_24_q, SlotData;

  Comparator #(.width(11), .mode("twosComplement")) comparator_1 (
    .a(TagData), .b(Addr[15:5]), .eq(comparator_1_eq));  // open: gt, lt
  assign Valid = L0 ? register_1_q : 1'bz;  // Controlled_Buffer controlled_buffer_1
  Register #(.width(1), .trigger("rising"), .Select("low")) register_1 (
    .D(1'b1), .en(and_2_out), .Q(register_1_q), .clk(CLK));  // open: clr
  assign Valid = L1 ? register_2_q : 1'bz;  // Controlled_Buffer controlled_buffer_2
  Register #(.width(1), .trigger("rising"), .Select("low")) register_2 (
    .D(1'b1), .en(and_3_out), .Q(register_2_q), .clk(CLK));  // open: clr
  Register #(.width(1), .trigger("rising"), .Select("low")) register_3 (
    .D(1'b1), .en(and_4_out), .Q(register_3_q), .clk(CLK));  // open: clr
  assign Valid = L2 ? register_3_q : 1'bz;  // Controlled_Buffer controlled_buffer_3
  Register #(.width(1), .trigger("rising"), .Select("low")) register_4 (
    .D(1'b1), .en(and_5_out), .Q(register_4_q), .clk(CLK));  // open: clr
  assign Valid = L3 ? register_4_q : 1'bz;  // Controlled_Buffer controlled_buffer_4
  assign Valid = L4 ? register_5_q : 1'bz;  // Controlled_Buffer controlled_buffer_5
  Register #(.width(1), .trigger("rising"), .Select("low")) register_5 (
    .D(1'b1), .en(and_6_out), .Q(register_5_q), .clk(CLK));  // open: clr
  Register #(.width(1), .trigger("rising"), .Select("low")) register_6 (
    .D(1'b1), .en(and_7_out), .Q(register_6_q), .clk(CLK));  // open: clr
  assign Valid = L5 ? register_6_q : 1'bz;  // Controlled_Buffer controlled_buffer_6
  assign Valid = L6 ? register_7_q : 1'bz;  // Controlled_Buffer controlled_buffer_7
  Register #(.width(1), .trigger("rising"), .Select("low")) register_7 (
    .D(1'b1), .en(and_8_out), .Q(register_7_q), .clk(CLK));  // open: clr
  Register #(.width(1), .trigger("rising"), .Select("low")) register_8 (
    .D(1'b1), .en(and_9_out), .Q(register_8_q), .clk(CLK));  // open: clr
  assign Valid = L7 ? register_8_q : 1'bz;  // Controlled_Buffer controlled_buffer_8
  and and_1 (Hit, Valid, comparator_1_eq);
  Multiplexer #(.select(2), .width(8), .disabled("Z"), .enable("true")) multiplexer_1 (
    .in0(SlotData[7:0]), .in1(SlotData[15:8]), .in2(SlotData[23:16]), .in3(SlotData[31:24]), .out(DataOut),
    .sel(Addr[1:0]), .en(Hit));
  not not_1 (Miss, Hit);
  Register #(.width(11), .trigger("rising"), .Select("low")) register_9 (
    .D(Addr[15:5]), .en(and_2_out), .Q(register_9_q), .clk(CLK));  // open: clr
  Register #(.width(11), .trigger("rising"), .Select("low")) register_10 (
    .D(Addr[15:5]), .en(and_3_out), .Q(register_10_q), .clk(CLK));  // open: clr
  Register #(.width(11), .trigger("rising"), .Select("low")) register_11 (
    .D(Addr[15:5]), .en(and_4_out), .Q(register_11_q), .clk(CLK));  // open: clr
  Register #(.width(11), .trigger("rising"), .Select("low")) register_12 (
    .D(Addr[15:5]), .en(and_5_out), .Q(register_12_q), .clk(CLK));  // open: clr
  Register #(.width(11), .trigger("rising"), .Select("low")) register_13 (
    .D(Addr[15:5]), .en(and_6_out), .Q(register_13_q), .clk(CLK));  // open: clr
  Register #(.width(11), .trigger("rising"), .Select("low")) register_14 (
    .D(Addr[15:5]), .en(and_7_out), .Q(register_14_q), .clk(CLK));  // open: clr
  Register #(.width(11), .trigger("rising"), .Select("low")) register_15 (
    .D(Addr[15:5]), .en(and_8_out), .Q(register_15_q), .clk(CLK));  // open: clr
  Register #(.width(11), .trigger("rising"), .Select("low")) register_16 (
    .D(Addr[15:5]), .en(and_9_out), .Q(register_16_q), .clk(CLK));  // open: clr
  Decoder #(.select(3), .tristate("false"), .disabled("Z"), .enable("false")) decoder_1 (
    .out0(L0), .out1(L1), .out2(L2), .out3(L3), .out4(L4), .out5(L5), .out6(L6), .out7(L7), .sel(Addr[4:2]));
  assign TagData = L0 ? register_9_q : 11'bz;  // Controlled_Buffer controlled_buffer_9
  assign TagData = L1 ? register_10_q : 11'bz;  // Controlled_Buffer controlled_buffer_10
  assign TagData = L2 ? register_11_q : 11'bz;  // Controlled_Buffer controlled_buffer_11
  assign TagData = L3 ? register_12_q : 11'bz;  // Controlled_Buffer controlled_buffer_12
  assign TagData = L4 ? register_13_q : 11'bz;  // Controlled_Buffer controlled_buffer_13
  assign TagData = L5 ? register_14_q : 11'bz;  // Controlled_Buffer controlled_buffer_14
  assign TagData = L6 ? register_15_q : 11'bz;  // Controlled_Buffer controlled_buffer_15
  assign TagData = L7 ? register_16_q : 11'bz;  // Controlled_Buffer controlled_buffer_16
  Register #(.width(32), .trigger("rising"), .Select("low")) register_17 (
    .D(BlockDataIn), .en(and_2_out), .Q(register_17_q), .clk(CLK));  // open: clr
  Register #(.width(32), .trigger("rising"), .Select("low")) register_18 (
    .D(BlockDataIn), .en(and_3_out), .Q(register_18_q), .clk(CLK));  // open: clr
  Register #(.width(32), .trigger("rising"), .Select("low")) register_19 (
    .D(BlockDataIn), .en(and_4_out), .Q(register_19_q), .clk(CLK));  // open: clr
  Register #(.width(32), .trigger("rising"), .Select("low")) register_20 (
    .D(BlockDataIn), .en(and_5_out), .Q(register_20_q), .clk(CLK));  // open: clr
  Register #(.width(32), .trigger("rising"), .Select("low")) register_21 (
    .D(BlockDataIn), .en(and_6_out), .Q(register_21_q), .clk(CLK));  // open: clr
  Register #(.width(32), .trigger("rising"), .Select("low")) register_22 (
    .D(BlockDataIn), .en(and_7_out), .Q(register_22_q), .clk(CLK));  // open: clr
  Register #(.width(32), .trigger("rising"), .Select("low")) register_23 (
    .D(BlockDataIn), .en(and_8_out), .Q(register_23_q), .clk(CLK));  // open: clr
  Register #(.width(32), .trigger("rising"), .Select("low")) register_24 (
    .D(BlockDataIn), .en(and_9_out), .Q(register_24_q), .clk(CLK));  // open: clr
  assign SlotData = L0 ? register_17_q : 32'bz;  // Controlled_Buffer controlled_buffer_17
  and and_2 (and_2_out, L0, BlkDataReady);
  assign SlotData = L1 ? register_18_q : 32'bz;  // Controlled_Buffer controlled_buffer_18
  and and_3 (and_3_out, L1, BlkDataReady);
  assign SlotData = L2 ? register_19_q : 32'bz;  // Controlled_Buffer controlled_buffer_19
  and and_4 (and_4_out, L2, BlkDataReady);
  assign SlotData = L3 ? register_20_q : 32'bz;  // Controlled_Buffer controlled_buffer_20
  and and_5 (and_5_out, L3, BlkDataReady);
  assign SlotData = L4 ? register_21_q : 32'bz;  // Controlled_Buffer controlled_buffer_21
  and and_6 (and_6_out, L4, BlkDataReady);
  assign SlotData = L5 ? register_22_q : 32'bz;  // Controlled_Buffer controlled_buffer_22
  and and_7 (and_7_out, L5, BlkDataReady);
  assign SlotData = L6 ? register_23_q : 32'bz;  // Controlled_Buffer controlled_buffer_23
  and and_8 (and_8_out, L6, BlkDataReady);
  assign SlotData = L7 ? register_24_q : 32'bz;  // Controlled_Buffer controlled_buffer_24
  and and_9 (and_9_out, L7, BlkDataReady);

  // Other names for the same wires on the sheet: Blk[31:0] = BlockDataIn; BlkReady = BlkDataReady; 字节地址[15:0] = Addr;
  //   Tag[10:0] = Addr[15:5]

  // Notes on the sheet:
  //   输入引脚区
  //   请勿增改引脚，请勿修改子电路封装
  //   电路功能：利用上面给定的隧道构建8行的Cache，cache映射方式自选
  //   请在下方利用上方输入输出引脚的隧道信号构建电路，ctrl+d复制选择部件
  //   输出引脚区
endmodule

module \Cache_全相联  (
  input  [31:0] BlockDataIn,
  input  [15:0] Addr,
  input  BlkDataReady,
  input  CLK,
  output Miss,
  output [7:0] DataOut
);

  wire and_1_out, and_2_out, and_3_out, and_4_out, and_5_out, and_6_out, and_7_out, and_8_out,
       comparator_1_eq, comparator_2_eq, comparator_3_eq, comparator_4_eq, comparator_5_eq, comparator_6_eq,
       comparator_7_eq, comparator_8_eq, Hit0, Hit1, Hit2, Hit3, Hit4, Hit5, Hit6, Hit7, or_1_out, or_2_out,
       or_3_out, or_4_out, or_5_out, or_6_out, or_7_out, or_8_out, or_9_out, Valid0, Valid1, Valid2, Valid3,
       Valid4, Valid5, Valid6, Valid7, Wirite0, Wirite1, Wirite2, Wirite3, Wirite4, Wirite5, Wirite6, Wirite7;
  wire [2:0] Index, max2_1_indexout, max2_2_indexout, max2_3_indexout, max2_4_indexout, max2_5_indexout,
       max2_6_indexout;
  wire [13:0] Tag0, Tag1, Tag2, Tag3, Tag4, Tag5, Tag6, Tag7;
  wire [15:0] Cnt0, Cnt1, Cnt2, Cnt3, Cnt4, Cnt5, Cnt6, Cnt7, max2_1_cntout, max2_2_cntout, max2_3_cntout,
       max2_4_cntout, max2_5_cntout, max2_6_cntout;
  wire [31:0] register_17_q, register_18_q, register_19_q, register_20_q, register_21_q, register_22_q,
       register_23_q, register_24_q, SlotData;

  Register #(.width(1), .trigger("rising"), .Select("low")) register_1 (
    .D(1'b1), .en(and_1_out), .Q(Valid0), .clk(CLK));  // open: clr
  Register #(.width(1), .trigger("rising"), .Select("low")) register_2 (
    .D(1'b1), .en(and_2_out), .Q(Valid1), .clk(CLK));  // open: clr
  Register #(.width(1), .trigger("rising"), .Select("low")) register_3 (
    .D(1'b1), .en(and_3_out), .Q(Valid2), .clk(CLK));  // open: clr
  Register #(.width(1), .trigger("rising"), .Select("low")) register_4 (
    .D(1'b1), .en(and_4_out), .Q(Valid3), .clk(CLK));  // open: clr
  Register #(.width(1), .trigger("rising"), .Select("low")) register_5 (
    .D(1'b1), .en(and_5_out), .Q(Valid4), .clk(CLK));  // open: clr
  Register #(.width(1), .trigger("rising"), .Select("low")) register_6 (
    .D(1'b1), .en(and_6_out), .Q(Valid5), .clk(CLK));  // open: clr
  Register #(.width(1), .trigger("rising"), .Select("low")) register_7 (
    .D(1'b1), .en(and_7_out), .Q(Valid6), .clk(CLK));  // open: clr
  Register #(.width(1), .trigger("rising"), .Select("low")) register_8 (
    .D(1'b1), .en(and_8_out), .Q(Valid7), .clk(CLK));  // open: clr
  Register #(.width(14), .trigger("rising"), .Select("low")) register_9 (
    .D(Addr[15:2]), .en(and_1_out), .Q(Tag0), .clk(CLK));  // open: clr
  Register #(.width(14), .trigger("rising"), .Select("low")) register_10 (
    .D(Addr[15:2]), .en(and_2_out), .Q(Tag1), .clk(CLK));  // open: clr
  Register #(.width(14), .trigger("rising"), .Select("low")) register_11 (
    .D(Addr[15:2]), .en(and_3_out), .Q(Tag2), .clk(CLK));  // open: clr
  Register #(.width(14), .trigger("rising"), .Select("low")) register_12 (
    .D(Addr[15:2]), .en(and_4_out), .Q(Tag3), .clk(CLK));  // open: clr
  Register #(.width(14), .trigger("rising"), .Select("low")) register_13 (
    .D(Addr[15:2]), .en(and_5_out), .Q(Tag4), .clk(CLK));  // open: clr
  Register #(.width(14), .trigger("rising"), .Select("low")) register_14 (
    .D(Addr[15:2]), .en(and_6_out), .Q(Tag5), .clk(CLK));  // open: clr
  Register #(.width(14), .trigger("rising"), .Select("low")) register_15 (
    .D(Addr[15:2]), .en(and_7_out), .Q(Tag6), .clk(CLK));  // open: clr
  Register #(.width(14), .trigger("rising"), .Select("low")) register_16 (
    .D(Addr[15:2]), .en(and_8_out), .Q(Tag7), .clk(CLK));  // open: clr
  Multiplexer #(.select(2), .width(8), .disabled("Z"), .enable("false")) multiplexer_1 (
    .in0(SlotData[7:0]), .in1(SlotData[15:8]), .in2(SlotData[23:16]), .in3(SlotData[31:24]), .out(DataOut),
    .sel(Addr[1:0]));
  Counter #(.width(16), .max('hffff), .ongoal("wrap"), .trigger("rising"), .behavior("new")) counter_1 (
    .load(or_1_out), .D({16{1'b0}}), .Q(Cnt0), .clk(CLK));  // open: count, carry, clr, preset, down
  or or_1 (or_1_out, Hit0, Wirite0);
  Counter #(.width(16), .max('hffff), .ongoal("wrap"), .trigger("rising"), .behavior("new")) counter_2 (
    .load(or_2_out), .D({16{1'b0}}), .Q(Cnt1), .clk(CLK));  // open: count, carry, clr, preset, down
  or or_2 (or_2_out, Hit1, Wirite1);
  Counter #(.width(16), .max('hffff), .ongoal("wrap"), .trigger("rising"), .behavior("new")) counter_3 (
    .load(or_3_out), .D({16{1'b0}}), .Q(Cnt2), .clk(CLK));  // open: count, carry, clr, preset, down
  or or_3 (or_3_out, Hit2, Wirite2);
  Counter #(.width(16), .max('hffff), .ongoal("wrap"), .trigger("rising"), .behavior("new")) counter_4 (
    .load(or_4_out), .D({16{1'b0}}), .Q(Cnt3), .clk(CLK));  // open: count, carry, clr, preset, down
  or or_4 (or_4_out, Hit3, Wirite3);
  Counter #(.width(16), .max('hffff), .ongoal("wrap"), .trigger("rising"), .behavior("new")) counter_5 (
    .load(or_5_out), .D({16{1'b0}}), .Q(Cnt4), .clk(CLK));  // open: count, carry, clr, preset, down
  or or_5 (or_5_out, Hit4, Wirite4);
  Counter #(.width(16), .max('hffff), .ongoal("wrap"), .trigger("rising"), .behavior("new")) counter_6 (
    .load(or_6_out), .D({16{1'b0}}), .Q(Cnt5), .clk(CLK));  // open: count, carry, clr, preset, down
  or or_6 (or_6_out, Hit5, Wirite5);
  Counter #(.width(16), .max('hffff), .ongoal("wrap"), .trigger("rising"), .behavior("new")) counter_7 (
    .load(or_7_out), .D({16{1'b0}}), .Q(Cnt6), .clk(CLK));  // open: count, carry, clr, preset, down
  or or_7 (or_7_out, Hit6, Wirite6);
  Counter #(.width(16), .max('hffff), .ongoal("wrap"), .trigger("rising"), .behavior("new")) counter_8 (
    .load(or_8_out), .D({16{1'b0}}), .Q(Cnt7), .clk(CLK));  // open: count, carry, clr, preset, down
  or or_8 (or_8_out, Hit7, Wirite7);
  assign SlotData = or_1_out ? register_17_q : 32'bz;  // Controlled_Buffer controlled_buffer_1
  Register #(.width(32), .trigger("rising"), .Select("low")) register_17 (
    .D(BlockDataIn), .en(and_1_out), .Q(register_17_q), .clk(CLK));  // open: clr
  and and_1 (and_1_out, Wirite0, BlkDataReady);
  Register #(.width(32), .trigger("rising"), .Select("low")) register_18 (
    .D(BlockDataIn), .en(and_2_out), .Q(register_18_q), .clk(CLK));  // open: clr
  assign SlotData = or_2_out ? register_18_q : 32'bz;  // Controlled_Buffer controlled_buffer_2
  and and_2 (and_2_out, Wirite1, BlkDataReady);
  Register #(.width(32), .trigger("rising"), .Select("low")) register_19 (
    .D(BlockDataIn), .en(and_3_out), .Q(register_19_q), .clk(CLK));  // open: clr
  assign SlotData = or_3_out ? register_19_q : 32'bz;  // Controlled_Buffer controlled_buffer_3
  and and_3 (and_3_out, Wirite2, BlkDataReady);
  assign SlotData = or_4_out ? register_20_q : 32'bz;  // Controlled_Buffer controlled_buffer_4
  Register #(.width(32), .trigger("rising"), .Select("low")) register_20 (
    .D(BlockDataIn), .en(and_4_out), .Q(register_20_q), .clk(CLK));  // open: clr
  and and_4 (and_4_out, Wirite3, BlkDataReady);
  assign SlotData = or_5_out ? register_21_q : 32'bz;  // Controlled_Buffer controlled_buffer_5
  Register #(.width(32), .trigger("rising"), .Select("low")) register_21 (
    .D(BlockDataIn), .en(and_5_out), .Q(register_21_q), .clk(CLK));  // open: clr
  and and_5 (and_5_out, Wirite4, BlkDataReady);
  assign SlotData = or_6_out ? register_22_q : 32'bz;  // Controlled_Buffer controlled_buffer_6
  Register #(.width(32), .trigger("rising"), .Select("low")) register_22 (
    .D(BlockDataIn), .en(and_6_out), .Q(register_22_q), .clk(CLK));  // open: clr
  and and_6 (and_6_out, Wirite5, BlkDataReady);
  assign SlotData = or_7_out ? register_23_q : 32'bz;  // Controlled_Buffer controlled_buffer_7
  Register #(.width(32), .trigger("rising"), .Select("low")) register_23 (
    .D(BlockDataIn), .en(and_7_out), .Q(register_23_q), .clk(CLK));  // open: clr
  and and_7 (and_7_out, Wirite6, BlkDataReady);
  Register #(.width(32), .trigger("rising"), .Select("low")) register_24 (
    .D(BlockDataIn), .en(and_8_out), .Q(register_24_q), .clk(CLK));  // open: clr
  assign SlotData = or_8_out ? register_24_q : 32'bz;  // Controlled_Buffer controlled_buffer_8
  and and_8 (and_8_out, Wirite7, BlkDataReady);
  Demultiplexer #(.select(3), .width(1), .tristate("false"), .disabled("Z"), .enable("false")) demultiplexer_1 (
    .out0(Wirite0), .out1(Wirite1), .out2(Wirite2), .out3(Wirite3), .out4(Wirite4), .out5(Wirite5),
    .out6(Wirite6), .out7(Wirite7), .in(Miss), .sel(Index));
  Comparator #(.width(14), .mode("twosComplement")) comparator_1 (
    .a(Addr[15:2]), .b(Tag0), .eq(comparator_1_eq));  // open: gt, lt
  Comparator #(.width(14), .mode("twosComplement")) comparator_2 (
    .a(Addr[15:2]), .b(Tag1), .eq(comparator_2_eq));  // open: gt, lt
  Comparator #(.width(14), .mode("twosComplement")) comparator_3 (
    .a(Addr[15:2]), .b(Tag2), .eq(comparator_3_eq));  // open: gt, lt
  Comparator #(.width(14), .mode("twosComplement")) comparator_4 (
    .a(Addr[15:2]), .b(Tag3), .eq(comparator_4_eq));  // open: gt, lt
  Comparator #(.width(14), .mode("twosComplement")) comparator_5 (
    .a(Addr[15:2]), .b(Tag4), .eq(comparator_5_eq));  // open: gt, lt
  Comparator #(.width(14), .mode("twosComplement")) comparator_6 (
    .a(Addr[15:2]), .b(Tag5), .eq(comparator_6_eq));  // open: gt, lt
  Comparator #(.width(14), .mode("twosComplement")) comparator_7 (
    .a(Addr[15:2]), .b(Tag6), .eq(comparator_7_eq));  // open: gt, lt
  Comparator #(.width(14), .mode("twosComplement")) comparator_8 (
    .a(Addr[15:2]), .b(Tag7), .eq(comparator_8_eq));  // open: gt, lt
  Max2 max2_1 (
    .Cnt1(Cnt0), .Cnt2(Cnt1), .Index2(3'b001), .Index1(3'b000), .CntOut(max2_1_cntout),
    .IndexOut(max2_1_indexout));
  Max2 max2_2 (
    .Cnt1(Cnt2), .Cnt2(Cnt3), .Index2(3'b011), .Index1(3'b010), .CntOut(max2_2_cntout),
    .IndexOut(max2_2_indexout));
  Max2 max2_3 (
    .Cnt1(Cnt4), .Cnt2(Cnt5), .Index2(3'b101), .Index1(3'b100), .CntOut(max2_3_cntout),
    .IndexOut(max2_3_indexout));
  Max2 max2_4 (
    .Cnt1(Cnt6), .Cnt2(Cnt7), .Index2(3'b111), .Index1(3'b110), .CntOut(max2_4_cntout),
    .IndexOut(max2_4_indexout));
  not not_1 (Miss, or_9_out);
  or or_9 (or_9_out, Hit0, Hit1, Hit2, Hit3, Hit4, Hit5, Hit6, Hit7);
  and and_9 (Hit0, Valid0, comparator_1_eq);
  and and_10 (Hit1, Valid1, comparator_2_eq);
  and and_11 (Hit2, Valid2, comparator_3_eq);
  and and_12 (Hit3, Valid3, comparator_4_eq);
  and and_13 (Hit4, Valid4, comparator_5_eq);
  and and_14 (Hit5, Valid5, comparator_6_eq);
  and and_15 (Hit6, Valid6, comparator_7_eq);
  and and_16 (Hit7, Valid7, comparator_8_eq);
  Max2 max2_5 (
    .Cnt1(max2_1_cntout), .Cnt2(max2_2_cntout), .Index2(max2_2_indexout), .Index1(max2_1_indexout),
    .CntOut(max2_5_cntout), .IndexOut(max2_5_indexout));
  Max2 max2_6 (
    .Cnt1(max2_3_cntout), .Cnt2(max2_4_cntout), .Index2(max2_4_indexout), .Index1(max2_3_indexout),
    .CntOut(max2_6_cntout), .IndexOut(max2_6_indexout));
  Max2 max2_7 (
    .Cnt1(max2_5_cntout), .Cnt2(max2_6_cntout), .Index2(max2_6_indexout), .Index1(max2_5_indexout),
    .IndexOut(Index));  // open: CntOut

  // Other names for the same wires on the sheet: Blk[31:0] = BlockDataIn; BlkReady = BlkDataReady;
  //   offset[1:0] = Addr[1:0]; 字节地址[15:0] = Addr; TagIn[13:0] = Addr[15:2]

  // Notes on the sheet:
  //   输入引脚区
  //   请勿增改引脚，请勿修改子电路封装
  //   电路功能：利用上面给定的隧道构建8行的Cache，cache映射方式自选
  //   请在下方利用上方输入输出引脚的隧道信号构建电路，ctrl+d复制选择部件
  //   输出引脚区
endmodule

module \Cache_2路组相联  (
  input  [31:0] BlockDataIn,
  input  [15:0] Addr,
  input  BlkDataReady,
  input  CLK,
  output Miss,
  output [7:0] DataOut
);

  wire and_1_out, and_2_out, and_3_out, and_4_out, and_5_out, and_6_out, and_7_out, and_8_out, Cache0,
       Cache1, Cache2, Cache3, comparator_1_eq, comparator_2_eq, Hit0, Hit1, or_1_out, or_2_out, or_3_out,
       or_4_out, or_5_out, or_6_out, or_7_out, or_8_out, or_9_out, register_1_q, register_2_q, register_3_q,
       register_4_q, register_5_q, register_6_q, register_7_q, register_8_q, Reset00, Reset01, Reset10,
       Reset11, Reset20, Reset21, Reset30, Reset31, Valid0, Valid1, Wirite0, Wirite1;
  wire [2:0] Index;
  wire [12:0] register_9_q, register_10_q, register_11_q, register_12_q, register_13_q, register_14_q,
       register_15_q, register_16_q, Tag0, Tag1;
  wire [15:0] Cnt0, Cnt1, counter_1_q, counter_2_q, counter_3_q, counter_4_q, counter_5_q, counter_6_q,
       counter_7_q, counter_8_q;
  wire [31:0] register_17_q, register_18_q, register_19_q, register_20_q, register_21_q, register_22_q,
       register_23_q, register_24_q, SlotData;

  assign Valid0 = Cache0 ? register_1_q : 1'bz;  // Controlled_Buffer controlled_buffer_1
  Register #(.width(1), .trigger("rising"), .Select("low")) register_1 (
    .D(1'b1), .en(and_1_out), .Q(register_1_q), .clk(CLK));  // open: clr
  assign Valid1 = Cache0 ? register_2_q : 1'bz;  // Controlled_Buffer controlled_buffer_2
  Register #(.width(1), .trigger("rising"), .Select("low")) register_2 (
    .D(1'b1), .en(and_2_out), .Q(register_2_q), .clk(CLK));  // open: clr
  Register #(.width(1), .trigger("rising"), .Select("low")) register_3 (
    .D(1'b1), .en(and_3_out), .Q(register_3_q), .clk(CLK));  // open: clr
  assign Valid0 = Cache1 ? register_3_q : 1'bz;  // Controlled_Buffer controlled_buffer_3
  assign Valid1 = Cache1 ? register_4_q : 1'bz;  // Controlled_Buffer controlled_buffer_4
  Register #(.width(1), .trigger("rising"), .Select("low")) register_4 (
    .D(1'b1), .en(and_4_out), .Q(register_4_q), .clk(CLK));  // open: clr
  assign Valid0 = Cache2 ? register_5_q : 1'bz;  // Controlled_Buffer controlled_buffer_5
  Register #(.width(1), .trigger("rising"), .Select("low")) register_5 (
    .D(1'b1), .en(and_5_out), .Q(register_5_q), .clk(CLK));  // open: clr
  Register #(.width(1), .trigger("rising"), .Select("low")) register_6 (
    .D(1'b1), .en(and_6_out), .Q(register_6_q), .clk(CLK));  // open: clr
  assign Valid1 = Cache2 ? register_6_q : 1'bz;  // Controlled_Buffer controlled_buffer_6
  Register #(.width(1), .trigger("rising"), .Select("low")) register_7 (
    .D(1'b1), .en(and_7_out), .Q(register_7_q), .clk(CLK));  // open: clr
  assign Valid0 = Cache3 ? register_7_q : 1'bz;  // Controlled_Buffer controlled_buffer_7
  assign Valid1 = Cache3 ? register_8_q : 1'bz;  // Controlled_Buffer controlled_buffer_8
  Register #(.width(1), .trigger("rising"), .Select("low")) register_8 (
    .D(1'b1), .en(and_8_out), .Q(register_8_q), .clk(CLK));  // open: clr
  Register #(.width(13), .trigger("rising"), .Select("low")) register_9 (
    .D({1'b0, Addr[15:4]}), .en(and_1_out), .Q(register_9_q), .clk(CLK));  // open: clr
  Register #(.width(13), .trigger("rising"), .Select("low")) register_10 (
    .D({1'b0, Addr[15:4]}), .en(and_2_out), .Q(register_10_q), .clk(CLK));  // open: clr
  Register #(.width(13), .trigger("rising"), .Select("low")) register_11 (
    .D({1'b0, Addr[15:4]}), .en(and_3_out), .Q(register_11_q), .clk(CLK));  // open: clr
  Register #(.width(13), .trigger("rising"), .Select("low")) register_12 (
    .D({1'b0, Addr[15:4]}), .en(and_4_out), .Q(register_12_q), .clk(CLK));  // open: clr
  Register #(.width(13), .trigger("rising"), .Select("low")) register_13 (
    .D({1'b0, Addr[15:4]}), .en(and_5_out), .Q(register_13_q), .clk(CLK));  // open: clr
  Register #(.width(13), .trigger("rising"), .Select("low")) register_14 (
    .D({1'b0, Addr[15:4]}), .en(and_6_out), .Q(register_14_q), .clk(CLK));  // open: clr
  Register #(.width(13), .trigger("rising"), .Select("low")) register_15 (
    .D({1'b0, Addr[15:4]}), .en(and_7_out), .Q(register_15_q), .clk(CLK));  // open: clr
  Register #(.width(13), .trigger("rising"), .Select("low")) register_16 (
    .D({1'b0, Addr[15:4]}), .en(and_8_out), .Q(register_16_q), .clk(CLK));  // open: clr
  assign Tag0 = Cache0 ? register_9_q : 13'bz;  // Controlled_Buffer controlled_buffer_9
  assign Tag1 = Cache0 ? register_10_q : 13'bz;  // Controlled_Buffer controlled_buffer_10
  assign Tag0 = Cache1 ? register_11_q : 13'bz;  // Controlled_Buffer controlled_buffer_11
  assign Tag1 = Cache1 ? register_12_q : 13'bz;  // Controlled_Buffer controlled_buffer_12
  assign Tag0 = Cache2 ? register_13_q : 13'bz;  // Controlled_Buffer controlled_buffer_13
  assign Tag1 = Cache2 ? register_14_q : 13'bz;  // Controlled_Buffer controlled_buffer_14
  assign Tag0 = Cache3 ? register_15_q : 13'bz;  // Controlled_Buffer controlled_buffer_15
  assign Tag1 = Cache3 ? register_16_q : 13'bz;  // Controlled_Buffer controlled_buffer_16
  Multiplexer #(.select(2), .width(8), .disabled("Z"), .enable("false")) multiplexer_1 (
    .in0(SlotData[7:0]), .in1(SlotData[15:8]), .in2(SlotData[23:16]), .in3(SlotData[31:24]), .out(DataOut),
    .sel(Addr[1:0]));
  assign Cnt0 = Cache0 ? counter_1_q : 16'bz;  // Controlled_Buffer controlled_buffer_17
  Counter #(.width(16), .max('hffff), .ongoal("wrap"), .trigger("rising"), .behavior("new")) counter_1 (
    .load(Reset00), .D({16{1'b0}}), .Q(counter_1_q), .clk(CLK));  // open: count, carry, clr, preset, down
  assign Cnt1 = Cache0 ? counter_2_q : 16'bz;  // Controlled_Buffer controlled_buffer_18
  Counter #(.width(16), .max('hffff), .ongoal("wrap"), .trigger("rising"), .behavior("new")) counter_2 (
    .load(Reset01), .D({16{1'b0}}), .Q(counter_2_q), .clk(CLK));  // open: count, carry, clr, preset, down
  Counter #(.width(16), .max('hffff), .ongoal("wrap"), .trigger("rising"), .behavior("new")) counter_3 (
    .load(Reset10), .D({16{1'b0}}), .Q(counter_3_q), .clk(CLK));  // open: count, carry, clr, preset, down
  assign Cnt0 = Cache1 ? counter_3_q : 16'bz;  // Controlled_Buffer controlled_buffer_19
  Counter #(.width(16), .max('hffff), .ongoal("wrap"), .trigger("rising"), .behavior("new")) counter_4 (
    .load(Reset11), .D({16{1'b0}}), .Q(counter_4_q), .clk(CLK));  // open: count, carry, clr, preset, down
  assign Cnt1 = Cache1 ? counter_4_q : 16'bz;  // Controlled_Buffer controlled_buffer_20
  Counter #(.width(16), .max('hffff), .ongoal("wrap"), .trigger("rising"), .behavior("new")) counter_5 (
    .load(Reset20), .D({16{1'b0}}), .Q(counter_5_q), .clk(CLK));  // open: count, carry, clr, preset, down
  assign Cnt0 = Cache2 ? counter_5_q : 16'bz;  // Controlled_Buffer controlled_buffer_21
  assign Cnt1 = Cache2 ? counter_6_q : 16'bz;  // Controlled_Buffer controlled_buffer_22
  Counter #(.width(16), .max('hffff), .ongoal("wrap"), .trigger("rising"), .behavior("new")) counter_6 (
    .load(Reset21), .D({16{1'b0}}), .Q(counter_6_q), .clk(CLK));  // open: count, carry, clr, preset, down
  Counter #(.width(16), .max('hffff), .ongoal("wrap"), .trigger("rising"), .behavior("new")) counter_7 (
    .load(Reset30), .D({16{1'b0}}), .Q(counter_7_q), .clk(CLK));  // open: count, carry, clr, preset, down
  assign Cnt0 = Cache3 ? counter_7_q : 16'bz;  // Controlled_Buffer controlled_buffer_23
  assign Cnt1 = Cache3 ? counter_8_q : 16'bz;  // Controlled_Buffer controlled_buffer_24
  Counter #(.width(16), .max('hffff), .ongoal("wrap"), .trigger("rising"), .behavior("new")) counter_8 (
    .load(Reset31), .D({16{1'b0}}), .Q(counter_8_q), .clk(CLK));  // open: count, carry, clr, preset, down
  Decoder #(.select(2), .tristate("false"), .disabled("Z"), .enable("false")) decoder_1 (
    .out0(Cache0), .out1(Cache1), .out2(Cache2), .out3(Cache3), .sel(Addr[3:2]));
  assign SlotData = Reset00 ? register_17_q : 32'bz;  // Controlled_Buffer controlled_buffer_25
  Register #(.width(32), .trigger("rising"), .Select("low")) register_17 (
    .D(BlockDataIn), .en(and_1_out), .Q(register_17_q), .clk(CLK));  // open: clr
  and and_1 (and_1_out, Wirite0, Cache0, BlkDataReady);
  assign SlotData = Reset01 ? register_18_q : 32'bz;  // Controlled_Buffer controlled_buffer_26
  Register #(.width(32), .trigger("rising"), .Select("low")) register_18 (
    .D(BlockDataIn), .en(and_2_out), .Q(register_18_q), .clk(CLK));  // open: clr
  and and_2 (and_2_out, Wirite1, Cache0, BlkDataReady);
  Register #(.width(32), .trigger("rising"), .Select("low")) register_19 (
    .D(BlockDataIn), .en(and_3_out), .Q(register_19_q), .clk(CLK));  // open: clr
  assign SlotData = Reset10 ? register_19_q : 32'bz;  // Controlled_Buffer controlled_buffer_27
  and and_3 (and_3_out, Wirite0, Cache1, BlkDataReady);
  Register #(.width(32), .trigger("rising"), .Select("low")) register_20 (
    .D(BlockDataIn), .en(and_4_out), .Q(register_20_q), .clk(CLK));  // open: clr
  assign SlotData = Reset11 ? register_20_q : 32'bz;  // Controlled_Buffer controlled_buffer_28
  and and_4 (and_4_out, Wirite1, Cache1, BlkDataReady);
  Register #(.width(32), .trigger("rising"), .Select("low")) register_21 (
    .D(BlockDataIn), .en(and_5_out), .Q(register_21_q), .clk(CLK));  // open: clr
  assign SlotData = Reset20 ? register_21_q : 32'bz;  // Controlled_Buffer controlled_buffer_29
  and and_5 (and_5_out, Wirite0, Cache2, BlkDataReady);
  assign SlotData = Reset21 ? register_22_q : 32'bz;  // Controlled_Buffer controlled_buffer_30
  Register #(.width(32), .trigger("rising"), .Select("low")) register_22 (
    .D(BlockDataIn), .en(and_6_out), .Q(register_22_q), .clk(CLK));  // open: clr
  and and_6 (and_6_out, Wirite1, Cache2, BlkDataReady);
  assign SlotData = Reset30 ? register_23_q : 32'bz;  // Controlled_Buffer controlled_buffer_31
  Register #(.width(32), .trigger("rising"), .Select("low")) register_23 (
    .D(BlockDataIn), .en(and_7_out), .Q(register_23_q), .clk(CLK));  // open: clr
  and and_7 (and_7_out, Wirite0, Cache3, BlkDataReady);
  Register #(.width(32), .trigger("rising"), .Select("low")) register_24 (
    .D(BlockDataIn), .en(and_8_out), .Q(register_24_q), .clk(CLK));  // open: clr
  assign SlotData = Reset31 ? register_24_q : 32'bz;  // Controlled_Buffer controlled_buffer_32
  and and_8 (and_8_out, Wirite1, Cache3, BlkDataReady);
  or or_1 (or_1_out, Wirite0, Hit0);
  and and_9 (Reset00, or_1_out, Cache0);
  or or_2 (or_2_out, Wirite0, Hit0);
  and and_10 (Reset20, or_2_out, Cache2);
  Demultiplexer #(.select(1), .width(1), .tristate("false"), .disabled("Z"), .enable("false")) demultiplexer_1 (
    .out0(Wirite0), .out1(Wirite1), .in(Miss), .sel(Index[0]));
  Comparator #(.width(13), .mode("twosComplement")) comparator_1 (
    .a({1'b0, Addr[15:4]}), .b(Tag0), .eq(comparator_1_eq));  // open: gt, lt
  Comparator #(.width(13), .mode("twosComplement")) comparator_2 (
    .a({1'b0, Addr[15:4]}), .b(Tag1), .eq(comparator_2_eq));  // open: gt, lt
  Max2 max2_1 (.Cnt1(Cnt0), .Cnt2(Cnt1), .Index2(3'b001), .Index1(3'b000), .IndexOut(Index));  // open: CntOut
  or or_3 (or_3_out, Hit0, Hit1);
  not not_1 (Miss, or_3_out);
  and and_11 (Hit0, Valid0, comparator_1_eq);
  and and_12 (Hit1, Valid1, comparator_2_eq);
  or or_4 (or_4_out, Wirite1, Hit1);
  and and_13 (Reset01, or_4_out, Cache0);
  or or_5 (or_5_out, Wirite1, Hit1);
  and and_14 (Reset21, or_5_out, Cache2);
  or or_6 (or_6_out, Wirite0, Hit0);
  and and_15 (Reset10, or_6_out, Cache1);
  or or_7 (or_7_out, Wirite0, Hit0);
  and and_16 (Reset30, or_7_out, Cache3);
  or or_8 (or_8_out, Wirite1, Hit1);
  and and_17 (Reset11, or_8_out, Cache1);
  or or_9 (or_9_out, Wirite1, Hit1);
  and and_18 (Reset31, or_9_out, Cache3);

  // Other names for the same wires on the sheet: Blk[31:0] = BlockDataIn; BlkReady = BlkDataReady;
  //   TagIn[11:0] = Addr[15:4]; 字节地址[15:0] = Addr; Blockoffset[1:0] = Addr[1:0]; Groupoffset[1:0] = Addr[3:2]

  // Notes on the sheet:
  //   输入引脚区
  //   请勿增改引脚，请勿修改子电路封装
  //   电路功能：利用上面给定的隧道构建8行的Cache，cache映射方式自选
  //   请在下方利用上方输入输出引脚的隧道信号构建电路，ctrl+d复制选择部件
  //   输出引脚区
endmodule

module \Cache_4路组相联  (
  input  [31:0] BlockDataIn,
  input  [15:0] Addr,
  input  BlkDataReady,
  input  CLK,
  output Miss,
  output [7:0] DataOut
);

  wire and_1_out, and_2_out, and_3_out, and_4_out, and_5_out, and_6_out, and_7_out, and_8_out, Cache0,
       Cache1, comparator_1_eq, comparator_2_eq, comparator_3_eq, comparator_4_eq, Hit0, Hit1, Hit2, Hit3,
       or_1_out, or_2_out, or_3_out, or_4_out, or_5_out, or_6_out, or_7_out, or_8_out, or_9_out,
       register_1_q, register_2_q, register_3_q, register_4_q, register_5_q, register_6_q, register_7_q,
       register_8_q, Reset00, Reset01, Reset02, Reset03, Reset10, Reset11, Reset12, Reset13, Valid0, Valid1,
       Valid2, Valid3, Wirite0, Wirite1, Wirite2, Wirite3;
  wire [2:0] Index, max2_1_indexout, max2_2_indexout;
  wire [12:0] register_9_q, register_10_q, register_11_q, register_12_q, register_13_q, register_14_q,
       register_15_q, register_16_q, Tag0, Tag1, Tag2, Tag3;
  wire [15:0] Cnt0, Cnt1, Cnt2, Cnt3, counter_1_q, counter_2_q, counter_3_q, counter_4_q, counter_5_q,
       counter_6_q, counter_7_q, counter_8_q, max2_1_cntout, max2_2_cntout, max2_3_cntout;
  wire [31:0] register_17_q, register_18_q, register_19_q, register_20_q, register_21_q, register_22_q,
       register_23_q, register_24_q, SlotData;

  Register #(.width(1), .trigger("rising"), .Select("low")) register_1 (
    .D(1'b1), .en(and_1_out), .Q(register_1_q), .clk(CLK));  // open: clr
  assign Valid0 = Cache0 ? register_1_q : 1'bz;  // Controlled_Buffer controlled_buffer_1
  assign Valid1 = Cache0 ? register_2_q : 1'bz;  // Controlled_Buffer controlled_buffer_2
  Register #(.width(1), .trigger("rising"), .Select("low")) register_2 (
    .D(1'b1), .en(and_2_out), .Q(register_2_q), .clk(CLK));  // open: clr
  assign Valid2 = Cache0 ? register_3_q : 1'bz;  // Controlled_Buffer controlled_buffer_3
  Register #(.width(1), .trigger("rising"), .Select("low")) register_3 (
    .D(1'b1), .en(and_3_out), .Q(register_3_q), .clk(CLK));  // open: clr
  assign Valid3 = Cache0 ? register_4_q : 1'bz;  // Controlled_Buffer controlled_buffer_4
  Register #(.width(1), .trigger("rising"), .Select("low")) register_4 (
    .D(1'b1), .en(and_4_out), .Q(register_4_q), .clk(CLK));  // open: clr
  Register #(.width(1), .trigger("rising"), .Select("low")) register_5 (
    .D(1'b1), .en(and_5_out), .Q(register_5_q), .clk(CLK));  // open: clr
  assign Valid0 = Cache1 ? register_5_q : 1'bz;  // Controlled_Buffer controlled_buffer_5
  assign Valid1 = Cache1 ? register_6_q : 1'bz;  // Controlled_Buffer controlled_buffer_6
  Register #(.width(1), .trigger("rising"), .Select("low")) register_6 (
    .D(1'b1), .en(and_6_out), .Q(register_6_q), .clk(CLK));  // open: clr
  assign Valid2 = Cache1 ? register_7_q : 1'bz;  // Controlled_Buffer controlled_buffer_7
  Register #(.width(1), .trigger("rising"), .Select("low")) register_7 (
    .D(1'b1), .en(and_7_out), .Q(register_7_q), .clk(CLK));  // open: clr
  Register #(.width(1), .trigger("rising"), .Select("low")) register_8 (
    .D(1'b1), .en(and_8_out), .Q(register_8_q), .clk(CLK));  // open: clr
  assign Valid3 = Cache1 ? register_8_q : 1'bz;  // Controlled_Buffer controlled_buffer_8
  Register #(.width(13), .trigger("rising"), .Select("low")) register_9 (
    .D(Addr[15:3]), .en(and_1_out), .Q(register_9_q), .clk(CLK));  // open: clr
  Register #(.width(13), .trigger("rising"), .Select("low")) register_10 (
    .D(Addr[15:3]), .en(and_2_out), .Q(register_10_q), .clk(CLK));  // open: clr
  Register #(.width(13), .trigger("rising"), .Select("low")) register_11 (
    .D(Addr[15:3]), .en(and_3_out), .Q(register_11_q), .clk(CLK));  // open: clr
  Register #(.width(13), .trigger("rising"), .Select("low")) register_12 (
    .D(Addr[15:3]), .en(and_4_out), .Q(register_12_q), .clk(CLK));  // open: clr
  Register #(.width(13), .trigger("rising"), .Select("low")) register_13 (
    .D(Addr[15:3]), .en(and_5_out), .Q(register_13_q), .clk(CLK));  // open: clr
  Register #(.width(13), .trigger("rising"), .Select("low")) register_14 (
    .D(Addr[15:3]), .en(and_6_out), .Q(register_14_q), .clk(CLK));  // open: clr
  Register #(.width(13), .trigger("rising"), .Select("low")) register_15 (
    .D(Addr[15:3]), .en(and_7_out), .Q(register_15_q), .clk(CLK));  // open: clr
  Register #(.width(13), .trigger("rising"), .Select("low")) register_16 (
    .D(Addr[15:3]), .en(and_8_out), .Q(register_16_q), .clk(CLK));  // open: clr
  assign Tag0 = Cache0 ? register_9_q : 13'bz;  // Controlled_Buffer controlled_buffer_9
  assign Tag1 = Cache0 ? register_10_q : 13'bz;  // Controlled_Buffer controlled_buffer_10
  assign Tag2 = Cache0 ? register_11_q : 13'bz;  // Controlled_Buffer controlled_buffer_11
  assign Tag3 = Cache0 ? register_12_q : 13'bz;  // Controlled_Buffer controlled_buffer_12
  assign Tag0 = Cache1 ? register_13_q : 13'bz;  // Controlled_Buffer controlled_buffer_13
  assign Tag1 = Cache1 ? register_14_q : 13'bz;  // Controlled_Buffer controlled_buffer_14
  assign Tag2 = Cache1 ? register_15_q : 13'bz;  // Controlled_Buffer controlled_buffer_15
  assign Tag3 = Cache1 ? register_16_q : 13'bz;  // Controlled_Buffer controlled_buffer_16
  Multiplexer #(.select(2), .width(8), .disabled("Z"), .enable("false")) multiplexer_1 (
    .in0(SlotData[7:0]), .in1(SlotData[15:8]), .in2(SlotData[23:16]), .in3(SlotData[31:24]), .out(DataOut),
    .sel(Addr[1:0]));
  Counter #(.width(16), .max('hffff), .ongoal("wrap"), .trigger("rising"), .behavior("new")) counter_1 (
    .load(Reset00), .D({16{1'b0}}), .Q(counter_1_q), .clk(CLK));  // open: count, carry, clr, preset, down
  assign Cnt0 = Cache0 ? counter_1_q : 16'bz;  // Controlled_Buffer controlled_buffer_17
  Counter #(.width(16), .max('hffff), .ongoal("wrap"), .trigger("rising"), .behavior("new")) counter_2 (
    .load(Reset01), .D({16{1'b0}}), .Q(counter_2_q), .clk(CLK));  // open: count, carry, clr, preset, down
  assign Cnt1 = Cache0 ? counter_2_q : 16'bz;  // Controlled_Buffer controlled_buffer_18
  assign Cnt2 = Cache0 ? counter_3_q : 16'bz;  // Controlled_Buffer controlled_buffer_19
  Counter #(.width(16), .max('hffff), .ongoal("wrap"), .trigger("rising"), .behavior("new")) counter_3 (
    .load(Reset02), .D({16{1'b0}}), .Q(counter_3_q), .clk(CLK));  // open: count, carry, clr, preset, down
  assign Cnt3 = Cache0 ? counter_4_q : 16'bz;  // Controlled_Buffer controlled_buffer_20
  Counter #(.width(16), .max('hffff), .ongoal("wrap"), .trigger("rising"), .behavior("new")) counter_4 (
    .load(Reset03), .D({16{1'b0}}), .Q(counter_4_q), .clk(CLK));  // open: count, carry, clr, preset, down
  Counter #(.width(16), .max('hffff), .ongoal("wrap"), .trigger("rising"), .behavior("new")) counter_5 (
    .load(Reset10), .D({16{1'b0}}), .Q(counter_5_q), .clk(CLK));  // open: count, carry, clr, preset, down
  assign Cnt0 = Cache1 ? counter_5_q : 16'bz;  // Controlled_Buffer controlled_buffer_21
  assign Cnt1 = Cache1 ? counter_6_q : 16'bz;  // Controlled_Buffer controlled_buffer_22
  Counter #(.width(16), .max('hffff), .ongoal("wrap"), .trigger("rising"), .behavior("new")) counter_6 (
    .load(Reset11), .D({16{1'b0}}), .Q(counter_6_q), .clk(CLK));  // open: count, carry, clr, preset, down
  assign Cnt2 = Cache1 ? counter_7_q : 16'bz;  // Controlled_Buffer controlled_buffer_23
  Counter #(.width(16), .max('hffff), .ongoal("wrap"), .trigger("rising"), .behavior("new")) counter_7 (
    .load(Reset12), .D({16{1'b0}}), .Q(counter_7_q), .clk(CLK));  // open: count, carry, clr, preset, down
  Counter #(.width(16), .max('hffff), .ongoal("wrap"), .trigger("rising"), .behavior("new")) counter_8 (
    .load(Reset13), .D({16{1'b0}}), .Q(counter_8_q), .clk(CLK));  // open: count, carry, clr, preset, down
  assign Cnt3 = Cache1 ? counter_8_q : 16'bz;  // Controlled_Buffer controlled_buffer_24
  Decoder #(.select(1), .tristate("false"), .disabled("Z"), .enable("false")) decoder_1 (
    .out0(Cache0), .out1(Cache1), .sel(Addr[2]));
  Register #(.width(32), .trigger("rising"), .Select("low")) register_17 (
    .D(BlockDataIn), .en(and_1_out), .Q(register_17_q), .clk(CLK));  // open: clr
  assign SlotData = Reset00 ? register_17_q : 32'bz;  // Controlled_Buffer controlled_buffer_25
  and and_1 (and_1_out, Wirite0, Cache0, BlkDataReady);
  assign SlotData = Reset01 ? register_18_q : 32'bz;  // Controlled_Buffer controlled_buffer_26
  Register #(.width(32), .trigger("rising"), .Select("low")) register_18 (
    .D(BlockDataIn), .en(and_2_out), .Q(register_18_q), .clk(CLK));  // open: clr
  and and_2 (and_2_out, Wirite1, Cache0, BlkDataReady);
  assign SlotData = Reset02 ? register_19_q : 32'bz;  // Controlled_Buffer controlled_buffer_27
  Register #(.width(32), .trigger("rising"), .Select("low")) register_19 (
    .D(BlockDataIn), .en(and_3_out), .Q(register_19_q), .clk(CLK));  // open: clr
  and and_3 (and_3_out, Wirite2, Cache0, BlkDataReady);
  Register #(.width(32), .trigger("rising"), .Select("low")) register_20 (
    .D(BlockDataIn), .en(and_4_out), .Q(register_20_q), .clk(CLK));  // open: clr
  assign SlotData = Reset03 ? register_20_q : 32'bz;  // Controlled_Buffer controlled_buffer_28
  and and_4 (and_4_out, Wirite3, Cache0, BlkDataReady);
  Register #(.width(32), .trigger("rising"), .Select("low")) register_21 (
    .D(BlockDataIn), .en(and_5_out), .Q(register_21_q), .clk(CLK));  // open: clr
  assign SlotData = Reset10 ? register_21_q : 32'bz;  // Controlled_Buffer controlled_buffer_29
  and and_5 (and_5_out, Wirite0, Cache1, BlkDataReady);
  Register #(.width(32), .trigger("rising"), .Select("low")) register_22 (
    .D(BlockDataIn), .en(and_6_out), .Q(register_22_q), .clk(CLK));  // open: clr
  assign SlotData = Reset11 ? register_22_q : 32'bz;  // Controlled_Buffer controlled_buffer_30
  and and_6 (and_6_out, Wirite1, Cache1, BlkDataReady);
  assign SlotData = Reset12 ? register_23_q : 32'bz;  // Controlled_Buffer controlled_buffer_31
  Register #(.width(32), .trigger("rising"), .Select("low")) register_23 (
    .D(BlockDataIn), .en(and_7_out), .Q(register_23_q), .clk(CLK));  // open: clr
  and and_7 (and_7_out, Wirite2, Cache1, BlkDataReady);
  assign SlotData = Reset13 ? register_24_q : 32'bz;  // Controlled_Buffer controlled_buffer_32
  Register #(.width(32), .trigger("rising"), .Select("low")) register_24 (
    .D(BlockDataIn), .en(and_8_out), .Q(register_24_q), .clk(CLK));  // open: clr
  and and_8 (and_8_out, Wirite3, Cache1, BlkDataReady);
  or or_1 (or_1_out, Wirite0, Hit0);
  and and_9 (Reset00, or_1_out, Cache0);
  or or_2 (or_2_out, Wirite0, Hit0);
  and and_10 (Reset10, or_2_out, Cache1);
  Demultiplexer #(.select(2), .width(1), .tristate("false"), .disabled("Z"), .enable("false")) demultiplexer_1 (
    .out0(Wirite0), .out1(Wirite1), .out2(Wirite2), .out3(Wirite3), .in(Miss), .sel(Index[1:0]));
  Comparator #(.width(13), .mode("twosComplement")) comparator_1 (
    .a(Addr[15:3]), .b(Tag0), .eq(comparator_1_eq));  // open: gt, lt
  Comparator #(.width(13), .mode("twosComplement")) comparator_2 (
    .a(Addr[15:3]), .b(Tag1), .eq(comparator_2_eq));  // open: gt, lt
  Comparator #(.width(13), .mode("twosComplement")) comparator_3 (
    .a(Addr[15:3]), .b(Tag2), .eq(comparator_3_eq));  // open: gt, lt
  Comparator #(.width(13), .mode("twosComplement")) comparator_4 (
    .a(Addr[15:3]), .b(Tag3), .eq(comparator_4_eq));  // open: gt, lt
  Max2 max2_1 (
    .Cnt1(Cnt0), .Cnt2(Cnt1), .Index2(3'b001), .Index1(3'b000), .CntOut(max2_1_cntout),
    .IndexOut(max2_1_indexout));
  Max2 max2_2 (
    .Cnt1(Cnt2), .Cnt2(Cnt3), .Index2(3'b011), .Index1(3'b010), .CntOut(max2_2_cntout),
    .IndexOut(max2_2_indexout));
  or or_3 (or_3_out, Hit0, Hit1, Hit2, Hit3);
  not not_1 (Miss, or_3_out);
  and and_11 (Hit0, Valid0, comparator_1_eq);
  and and_12 (Hit1, Valid1, comparator_2_eq);
  and and_13 (Hit2, Valid2, comparator_3_eq);
  and and_14 (Hit3, Valid3, comparator_4_eq);
  or or_4 (or_4_out, Wirite1, Hit1);
  and and_15 (Reset01, or_4_out, Cache0);
  or or_5 (or_5_out, Wirite1, Hit1);
  and and_16 (Reset11, or_5_out, Cache1);
  Max2 max2_3 (
    .Cnt1(max2_1_cntout), .Cnt2(max2_2_cntout), .Index2(max2_2_indexout), .Index1(max2_1_indexout),
    .CntOut(max2_3_cntout), .IndexOut(Index));
  or or_6 (or_6_out, Wirite2, Hit2);
  and and_17 (Reset02, or_6_out, Cache0);
  or or_7 (or_7_out, Wirite2, Hit2);
  and and_18 (Reset12, or_7_out, Cache1);
  or or_8 (or_8_out, Wirite3, Hit3);
  and and_19 (Reset03, or_8_out, Cache0);
  or or_9 (or_9_out, Wirite3, Hit3);
  and and_20 (Reset13, or_9_out, Cache1);

  // Other names for the same wires on the sheet: Blk[31:0] = BlockDataIn; BlkReady = BlkDataReady;
  //   Blockoffset[1:0] = Addr[1:0]; 字节地址[15:0] = Addr; Groupoffset = Addr[2]; TagIn[12:0] = Addr[15:3]

  // Notes on the sheet:
  //   输入引脚区
  //   请勿增改引脚，请勿修改子电路封装
  //   电路功能：利用上面给定的隧道构建8行的Cache，cache映射方式自选
  //   请在下方利用上方输入输出引脚的隧道信号构建电路，ctrl+d复制选择部件
  //   输出引脚区
endmodule

module \Cache自动测试  (
  input  in_1
);

  wire and_2_out, Clk, comparator_1_lt, comparator_2_eq, comparator_3_eq, controlled_buffer_1_out, EN, Error,
       Go, Hit, Miss, or_1_out, RDY, Runing;
  wire [3:0] _1, _2, _3;
  wire [7:0] Dataout, rom_2_data;
  wire [9:0] \计数器_q ;
  wire [15:0] adder_1_out, Addr, bit_extender_3_out, \cache块交换_1_byteaddrout , counter_1_q, subtractor_1_out,
       \实际命中 , \时钟周期数 , \校验和 , \缺失次数 , \访问次数 ;
  wire [31:0] bit_extender_1_out, bit_extender_2_out, \cache块交换_1_blockdatain , divider_1_out, divider_2_out,
       multiplier_1_out;
  wire [31:4] divider_2_rem, divider_3_out, divider_3_rem;

  Clock #(.highDuration(1), .lowDuration(1)) clock_1 (.out(Clk));
  // Probe on \实际命中 
  // Probe on \时钟周期数 
  not not_1 (Hit, Miss);
  Counter #(.width(10), .max('h3ff), .ongoal("wrap"), .trigger("rising"), .behavior("old")) \u_计数器  (
    .count(EN), .Q(\计数器_q ), .clk(Clk));  // open: load, D, carry, clr, preset
  and and_1 (EN, Hit, Go);
  and and_2 (and_2_out, Miss, RDY, Runing);
  // Probe on \计数器_q 
  Counter #(.width(16), .max('hffff), .ongoal("wrap"), .trigger("rising"), .behavior("old")) counter_1 (
    .count(and_2_out), .Q(counter_1_q), .clk(Clk));  // open: load, D, carry, clr, preset
  Subtractor #(.width(16)) subtractor_1 (.a(\访问次数 ), .b(\缺失次数 ), .out(subtractor_1_out));  // open: bin, bout
  Comparator #(.width(16), .mode("twosComplement")) comparator_1 (
    .a(\访问次数 ), .b(\缺失次数 ), .lt(comparator_1_lt));  // open: gt, eq
  not not_2 (Runing, comparator_2_eq);
  Comparator #(.width(10), .mode("twosComplement")) comparator_2 (
    .a(\计数器_q ), .b(10'h100), .eq(comparator_2_eq));  // open: gt, lt
  Register #(.width(16), .trigger("rising"), .Select("low")) register_1 (
    .D(counter_1_q), .en(EN), .Q(\缺失次数 ), .clk(Clk));  // open: clr
  Multiplexer #(.select(1), .width(16), .disabled(0), .enable("false")) multiplexer_1 (
    .in0(subtractor_1_out), .in1({16{1'b0}}), .out(\实际命中 ), .sel(comparator_1_lt));
  // Probe on \缺失次数 
  // Probe on \校验和 
  ROM #(.addrWidth(10), .dataWidth(16), .Select("high")) rom_1 (.addr(\计数器_q ), .data(Addr));
  Counter #(.width(16), .max('hffff), .ongoal("wrap"), .trigger("rising"), .behavior("old")) counter_2 (
    .count(EN), .Q(\访问次数 ), .clk(Clk));  // open: load, D, carry, clr, preset
  // Probe on Dataout
  assign bit_extender_1_out = {{16{1'b0}}, \实际命中 };  // Bit_Extender bit_extender_1
  // Probe on \访问次数 
  \Cache_2路组相联  \cache_2路组相联_1  (
    .BlockDataIn(\cache块交换_1_blockdatain ), .Addr(Addr), .BlkDataReady(RDY), .CLK(Clk), .Miss(Miss),
    .DataOut(Dataout));
  Multiplier #(.width(32)) multiplier_1 (
    .a(bit_extender_1_out), .b(32'h64), .out(multiplier_1_out));  // open: cin, cout
  assign bit_extender_2_out = {{16{1'b0}}, \访问次数 };  // Bit_Extender bit_extender_2
  assign bit_extender_3_out = {{8{1'b0}}, Dataout};  // Bit_Extender bit_extender_3
  Divider #(.width(32)) divider_1 (
    .a(multiplier_1_out), .b(bit_extender_2_out), .out(divider_1_out));  // open: upper, rem
  LED #(.active("true")) \u_读数据出错  (.in(Error));
  Pull_Resistor #(.pull(1)) pull_resistor_1 (.node(Miss));
  LED #(.active("true")) \u_缺失  (.in(Miss));
  Adder #(.width(16)) adder_1 (.a(\校验和 ), .b(bit_extender_3_out), .out(adder_1_out));  // open: cin, cout
  Hex_Digit_Display hex_digit_display_1 (.value(_3), .dp(1'b1));
  \Cache块交换  \cache块交换_1  (
    .Addr(Addr), .CLK(Clk), .ByteAddrOut(\cache块交换_1_byteaddrout ), .ByteDataIn(rom_2_data), .Miss(Miss),
    .BlkDataReady(RDY), .BlockDataIn(\cache块交换_1_blockdatain ), .Enable(Runing));
  Register #(.width(16), .trigger("rising"), .Select("low")) \u_校验和  (
    .D(adder_1_out), .en(EN), .Q(\校验和 ), .clk(Clk));  // open: clr
  Divider #(.width(32)) divider_2 (
    .a(divider_1_out), .b(32'ha), .out(divider_2_out), .rem({divider_2_rem, _1}));  // open: upper
  Hex_Digit_Display hex_digit_display_2 (.value(_1));  // open: dp
  Hex_Digit_Display hex_digit_display_3 (.value(_2));  // open: dp
  Divider #(.width(32)) divider_3 (
    .a(divider_2_out), .b(32'ha), .out({divider_3_out, _3}), .rem({divider_3_rem, _2}));  // open: upper
  ROM #(.addrWidth(16), .dataWidth(8), .Select("high")) rom_2 (.addr(\cache块交换_1_byteaddrout ), .data(rom_2_data));
  Comparator #(.width(8), .mode("twosComplement")) comparator_3 (
    .a(Addr[7:0]), .b(Dataout), .eq(comparator_3_eq));  // open: gt, lt
  assign controlled_buffer_1_out = Hit ? comparator_3_eq : 1'bz;  // Controlled_Buffer controlled_buffer_1
  Pull_Resistor #(.pull(1)) pull_resistor_2 (.node(controlled_buffer_1_out));
  or or_1 (or_1_out, controlled_buffer_1_out, ~in_1);  // OR_Gate
  not not_3 (Error, or_1_out);
  Counter #(.width(16), .max('hffff), .ongoal("wrap"), .trigger("rising"), .behavior("old")) counter_3 (
    .count(Runing), .Q(\时钟周期数 ), .clk(Clk));  // open: load, D, carry, clr, preset
  and and_3 (Go, Runing, or_1_out);

  // Other names for the same wires on the sheet: 读错误暂停 = in_1

  // Notes on the sheet:
  //   Trace存储器
  //   电路功能：测试Cache模块， ctrl+k启动时钟后，会自动对cache模块进行读数据测试，并将数据逐一读出进行校验和计算
  //   contents of rom_1 (hex, n*v repeats v):
  //   0 1 2 3 8 9 a b 10 11 12 13 20 21 22 23 8 9 a b 4 5 6 7 24 25 26 27 4 5 6 7 0 1 2 3 8 9 a b 8 9 a b
  //   20 21 22 23 28 29 2a 2b 24 25 26 27 4 5 6 7 24 25 26 27 0 1 2 3 8 9 a b 20 21 22 23 20 21 22 23 30
  //   31 32 33 4 5 6 7 24 25 26 27 4 5 6 7 0 1 2 3 8 9 a b 20 21 22 23 20 21 22 23 28 29 2a 2b 4 5 6 7 24
  //   2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
  //   如果设计了不同的映射方式，可以将该电路中cache模块替换为对应Cache模块即可!
  //   ctrl+r复位，  错误暂停模式位为1时，数据命中但读出数据不正确时会暂停系统
  //   默认trace是顺序访问，所以测试系统中判断读错误的逻辑是地址和数据相等，如果更换了trace，这个逻辑不正确
  //   参数统计区
  //   命中率
  //   电路状态稳定后显示最终命中率
  //   二级存储器
  //   Cache模拟器
  //   contents of rom_2 (hex, n*v repeats v):
  //   0 1 2 3 4 5 6 7 8 9 a b c d e f 10 11 12 13 14 15 16 17 18 19 1a 1b 1c 1d 1e 1f 20 21 22 23 24 25 26
  //   27 28 29 2a 2b 2c 2d 2e 2f 30 31 32 33 34 35 36 37 38 39 3a 3b 3c 3d 3e 3f 40 41 42 43 44 45 46 47
  //   48 49 4a 4b 4c 4d 4e 4f 50 51 52 53 54 55 56 57 58 59 5a 5b 5c 5d 5e 5f 60 61 62 63 64 65 66 67 68 6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
endmodule

// Max2
module \Max2_归并比较  (
  input  [15:0] Y,
  input  [15:0] X,
  input  [1:0] Y_num,
  input  [1:0] X_num,
  output [15:0] MAX,
  output [1:0] MAX_num
);

  wire comparator_1_eq, comparator_1_gt, or_1_out;

  Multiplexer #(.select(1), .width(16), .disabled("Z"), .enable("true")) multiplexer_1 (
    .in0(Y), .in1(X), .out(MAX), .sel(or_1_out), .en(1'b1));
  Comparator #(.width(16), .mode("unsigned")) comparator_1 (
    .a(X), .b(Y), .gt(comparator_1_gt), .eq(comparator_1_eq));  // open: lt
  or or_1 (or_1_out, comparator_1_gt, comparator_1_eq);
  Multiplexer #(.select(1), .width(2), .disabled("Z"), .enable("false")) multiplexer_2 (
    .in0(Y_num), .in1(X_num), .out(MAX_num), .sel(or_1_out));

  // Notes on the sheet:
  //   输出两个输入中的较大值，并输出较大值的2位编号
endmodule

// Max3
module \Max3_归并比较  (
  input  [15:0] Y,
  input  [15:0] X,
  input  [2:0] Y_num,
  input  [2:0] X_num,
  output [15:0] MAX,
  output [2:0] Max_num
);

  wire comparator_1_eq, comparator_1_gt, or_1_out;

  Multiplexer #(.select(1), .width(16), .disabled("Z"), .enable("false")) multiplexer_1 (
    .in0(Y), .in1(X), .out(MAX), .sel(or_1_out));
  Comparator #(.width(16), .mode("unsigned")) comparator_1 (
    .a(X), .b(Y), .gt(comparator_1_gt), .eq(comparator_1_eq));  // open: lt
  or or_1 (or_1_out, comparator_1_gt, comparator_1_eq);
  Multiplexer #(.select(1), .width(3), .disabled("Z"), .enable("false")) multiplexer_2 (
    .in0(Y_num), .in1(X_num), .out(Max_num), .sel(or_1_out));

  // Notes on the sheet:
  //   输出两个输入中的较大值，并输出较大值的3位编号
endmodule

module \Cache块交换  (
  input  [15:0] Addr,
  input  [7:0] ByteDataIn,
  input  Miss,
  input  Enable,
  input  CLK,
  output [15:0] ByteAddrOut,
  output [31:0] BlockDataIn,
  output BlkDataReady
);

  wire \块交换状态机_1_byte0_ready , \块交换状态机_1_byte1_ready , \块交换状态机_1_byte2_ready , \块交换状态机_1_byte3_ready ;
  wire [7:0] register_1_q, register_2_q, register_3_q, register_4_q;

  assign ByteAddrOut = \块交换状态机_1_byte0_ready  ? {Addr[15:2], 2'b00} : 16'bz;  // Controlled_Buffer controlled_buffer_1
  \块交换状态机  \u_块交换状态机_1  (
    .Clk(CLK), .Miss(Miss), .Byte0_Ready(\块交换状态机_1_byte0_ready ), .Byte1_Ready(\块交换状态机_1_byte1_ready ),
    .Byte2_Ready(\块交换状态机_1_byte2_ready ), .Byte3_Ready(\块交换状态机_1_byte3_ready ), .Byte0_Ready_2(BlkDataReady),
    .En(Enable));
  assign ByteAddrOut = \块交换状态机_1_byte1_ready  ? {Addr[15:2], 2'b01} : 16'bz;  // Controlled_Buffer controlled_buffer_2
  assign ByteAddrOut = \块交换状态机_1_byte2_ready  ? {Addr[15:2], 2'b10} : 16'bz;  // Controlled_Buffer controlled_buffer_3
  assign ByteAddrOut = \块交换状态机_1_byte3_ready  ? {Addr[15:2], 2'b11} : 16'bz;  // Controlled_Buffer controlled_buffer_4
  Register #(.width(8), .trigger("rising"), .Select("low")) register_1 (
    .D(ByteDataIn), .en(\块交换状态机_1_byte0_ready ), .Q(register_1_q), .clk(CLK));  // open: clr
  Register #(.width(8), .trigger("rising"), .Select("low")) register_2 (
    .D(ByteDataIn), .en(\块交换状态机_1_byte1_ready ), .Q(register_2_q), .clk(CLK));  // open: clr
  Register #(.width(8), .trigger("rising"), .Select("low")) register_3 (
    .D(ByteDataIn), .en(\块交换状态机_1_byte2_ready ), .Q(register_3_q), .clk(CLK));  // open: clr
  Register #(.width(8), .trigger("rising"), .Select("low")) register_4 (
    .D(ByteDataIn), .en(\块交换状态机_1_byte3_ready ), .Q(register_4_q), .clk(CLK));  // open: clr
  assign BlockDataIn = BlkDataReady ? {register_4_q, register_3_q, register_2_q, register_1_q} : 32'bz;  // Controlled_Buffer controlled_buffer_5

  // Notes on the sheet:
  //   数据缓存寄存器
endmodule
// 状态机
module \块交换状态机  (
  input  En,
  input  Clk,
  input  Miss,
  output Byte0_Ready,
  output Byte1_Ready,
  output Byte2_Ready,
  output Byte3_Ready,
  output Byte0_Ready_2
);

  wire and_1_out, and_2_out, and_3_out, and_4_out, and_5_out, and_6_out, and_7_out, Next_Q0, Next_Q1,
       Next_Q2, Next_Q3, not_1_out, not_2_out, not_3_out, not_4_out, not_5_out, not_6_out, not_7_out,
       not_8_out, not_9_out, not_10_out, not_11_out, not_12_out, not_13_out, or_1_out, or_2_out, Q0, Q1, Q2,
       Q3;

  not not_1 (not_1_out, Q3);
  not not_2 (not_2_out, Q3);
  not not_3 (not_3_out, Q2);
  not not_4 (not_4_out, Q3);
  not not_5 (not_5_out, Q1);
  not not_6 (not_6_out, Q3);
  not not_7 (not_7_out, Q0);
  not not_8 (not_8_out, Q3);
  not not_9 (not_9_out, Q0);
  D_Flip_Flop #(.trigger("rising"), .Pre_Clr_Positions("LEGACY"), .NegatePresetClear("false"), .enable("true"), .NewFFLayout("false")) d_ff_1 (
    .clk(Clk), .D(Next_Q3), .Q(Q3), .en(En));  // open: Qn, preset, reset
  D_Flip_Flop #(.trigger("rising"), .Pre_Clr_Positions("LEGACY"), .NegatePresetClear("false"), .enable("true"), .NewFFLayout("false")) d_ff_2 (
    .clk(Clk), .D(Next_Q2), .Q(Q2), .en(En));  // open: Qn, preset, reset
  D_Flip_Flop #(.trigger("rising"), .Pre_Clr_Positions("LEGACY"), .NegatePresetClear("false"), .enable("true"), .NewFFLayout("false")) d_ff_3 (
    .clk(Clk), .D(Next_Q1), .Q(Q1), .en(En));  // open: Qn, preset, reset
  D_Flip_Flop #(.trigger("rising"), .Pre_Clr_Positions("LEGACY"), .NegatePresetClear("false"), .enable("true"), .NewFFLayout("false")) d_ff_4 (
    .clk(Clk), .D(Next_Q0), .Q(Q0), .en(En));  // open: Qn, preset, reset
  and and_1 (and_1_out, not_1_out, Q2, Q1, Q0);
  and and_2 (and_2_out, not_2_out, not_3_out, Q1, Q0);
  not not_10 (not_10_out, Q3);
  and and_3 (and_3_out, not_10_out, Q2, not_11_out);
  not not_11 (not_11_out, Q1);
  not not_12 (not_12_out, Q3);
  and and_4 (and_4_out, not_12_out, Q2, not_13_out);
  not not_13 (not_13_out, Q0);
  and and_5 (and_5_out, not_4_out, not_5_out, Q0);
  and and_6 (and_6_out, not_6_out, Q1, not_7_out);
  and and_7 (and_7_out, not_8_out, not_9_out);
  or or_1 (or_1_out, and_2_out, and_3_out, and_4_out);
  or or_2 (or_2_out, and_5_out, and_6_out);
  Decoder #(.select(4), .tristate("false"), .disabled(0), .enable("false")) decoder_1 (
    .out1(Byte0_Ready), .out3(Byte1_Ready), .out5(Byte2_Ready), .out7(Byte3_Ready), .out8(Byte0_Ready_2),
    .sel({Q3, Q2, Q1, Q0}));  // open: out0, out2, out4, out6, out9, out10, out11, out12, out13, out14, out15
  and and_8 (Next_Q3, and_1_out, Miss);
  and and_9 (Next_Q2, or_1_out, Miss);
  and and_10 (Next_Q1, Miss, or_2_out);
  and and_11 (Next_Q0, Miss, and_7_out);
endmodule

// 评分
module \Regfile评分逻辑  (
  input  EQ,
  input  EN,
  input  CLK,
  output [31:0] \正确条数 ,
  output [3:0] High,
  output [3:0] Low,
  output [3:0] Mid,
  output [31:0] Total,
  output Right
);

  wire and_1_out, priority_encoder_1_gs, priority_encoder_1_out;
  wire [31:0] divider_1_out, divider_2_out, multiplier_1_out;
  wire [31:4] divider_2_rem, divider_3_out, divider_3_rem;

  Counter #(.width(32), .max('hffffffff), .ongoal("wrap"), .trigger("rising"), .behavior("old")) counter_1 (
    .count(EN), .Q(Total), .clk(CLK));  // open: load, D, carry, clr, preset
  Priority_Encoder #(.select(1), .disabled("Z")) priority_encoder_1 (
    .in0(EQ), .in1(EQ), .out(priority_encoder_1_out), .gs(priority_encoder_1_gs));  // open: en_out, en_in
  and and_1 (and_1_out, priority_encoder_1_out, priority_encoder_1_gs, EN);
  Counter #(.width(32), .max('hffffffff), .ongoal("wrap"), .trigger("rising"), .behavior("old")) counter_2 (
    .count(and_1_out), .Q(\正确条数 ), .clk(CLK));  // open: load, D, carry, clr, preset
  Multiplier #(.width(32)) multiplier_1 (.a(\正确条数 ), .b(32'h64), .out(multiplier_1_out));  // open: cin, cout
  Divider #(.width(32)) divider_1 (.a(multiplier_1_out), .b(Total), .out(divider_1_out));  // open: upper, rem
  Comparator #(.width(32), .mode("twosComplement")) comparator_1 (.a(\正确条数 ), .b(Total), .eq(Right));  // open: gt, lt
  Divider #(.width(32)) divider_2 (
    .a(divider_1_out), .b(32'ha), .out(divider_2_out), .rem({divider_2_rem, Low}));  // open: upper
  Divider #(.width(32)) divider_3 (
    .a(divider_2_out), .b(32'ha), .out({divider_3_out, High}), .rem({divider_3_rem, Mid}));  // open: upper

  // Notes on the sheet:
  //   只有使用优先编码器才能屏蔽掉位置状态
endmodule

module \子电路外观测试  (
);

  wire \cache_2路组相联_1_miss , \cache_4路组相联_1_miss , \cache_全相联_1_miss , \cache_直接相联_1_miss , undriven_4,
       undriven_6, undriven_10, undriven_11, undriven_13, undriven_14, undriven_20, undriven_22, undriven_24,
       undriven_25, undriven_27, undriven_29;
  wire [1:0] undriven_15;
  wire [4:0] undriven_17, undriven_18, undriven_19;
  wire [6:0] undriven_2, undriven_3;
  wire [7:0] \cache_2路组相联_1_dataout , \cache_4路组相联_1_dataout , \cache_全相联_1_dataout , \cache_直接相联_1_dataout ;
  wire [11:0] undriven_8;
  wire [15:0] undriven, undriven_7, undriven_16, undriven_26;
  wire [31:0] mips_ram_1_dataout, mips_regfile_1_reg1out, mips_regfile_1_reg2out, undriven_5, undriven_9,
       undriven_12, undriven_21, undriven_23, undriven_28, \字库电路_1_d0 , \字库电路_1_d1 , \字库电路_1_d3 ,
       \字库电路_1_d4 , \字库电路_1_d5 , \字库电路_1_d6 , \字库电路_1_d6_2 , \字库电路_1_d7 ;

  \字库电路  \u_字库电路_1  (
    .D0(\字库电路_1_d0 ), .D1(\字库电路_1_d1 ), .D6(\字库电路_1_d6 ), .D3(\字库电路_1_d3 ), .\区号 (undriven_2),
    .\位号 (undriven_3), .D4(\字库电路_1_d4 ), .D5(\字库电路_1_d5 ), .D6_2(\字库电路_1_d6_2 ), .D7(\字库电路_1_d7 ));
  \Cache_直接相联  \cache_直接相联_1  (
    .Addr(undriven), .CLK(undriven_4), .Miss(\cache_直接相联_1_miss ), .BlkDataReady(undriven_6),
    .DataOut(\cache_直接相联_1_dataout ), .BlockDataIn(undriven_5));
  MIPS_RAM mips_ram_1 (
    .\字节地址 (undriven_8), .Din(undriven_9), .DataOut(mips_ram_1_dataout), .CLK(undriven_14), .WE(undriven_11),
    .Mode(undriven_15));
  \Cache_全相联  \cache_全相联_1  (
    .BlockDataIn(undriven_12), .Addr(undriven_7), .BlkDataReady(undriven_13), .CLK(undriven_10),
    .Miss(\cache_全相联_1_miss ), .DataOut(\cache_全相联_1_dataout ));
  \Cache_2路组相联  \cache_2路组相联_1  (
    .BlockDataIn(undriven_23), .Addr(undriven_16), .BlkDataReady(undriven_24), .CLK(undriven_20),
    .Miss(\cache_2路组相联_1_miss ), .DataOut(\cache_2路组相联_1_dataout ));
  MIPS_Regfile mips_regfile_1 (
    .R1_num(undriven_17), .R2_num(undriven_18), .Write_Reg_num(undriven_19), .Din(undriven_21),
    .Write_Enable(undriven_22), .Clock(undriven_25), .Reg1Out(mips_regfile_1_reg1out),
    .Reg2Out(mips_regfile_1_reg2out));
  \Cache_4路组相联  \cache_4路组相联_1  (
    .BlockDataIn(undriven_28), .Addr(undriven_26), .BlkDataReady(undriven_29), .CLK(undriven_27),
    .Miss(\cache_4路组相联_1_miss ), .DataOut(\cache_4路组相联_1_dataout ));

  // Notes on the sheet:
  //   区号
  //   位号
  //   字库电路封装测试
  //   cache封装测试
  //   D0
  //   D1
  //   D2
  //   D3
  //   D4
  //   D5
  //   D6
  //   D7
  //   最好通过引脚悬浮提示看看连接是否正确，如果有问题，请调整封装引脚位置直至连接正确
  //   MIPS RAM电路封装测试
  //   请勿在子电路中增删改，甚至移动引脚位置，这些都可能导致子电路外观---封装发生改变，从而使得测试电路无法正确测试
  //   提交EduCoder平台检测之前，请先检查一下对应子电路的封装连接是否正确，主要查看引脚位置是否连接正确，有否错位未连接等情况
  //   MIPS寄存器文件电路封装测试
endmodule

module Max2 (
  input  [15:0] Cnt1,
  input  [15:0] Cnt2,
  input  [2:0] Index2,
  input  [2:0] Index1,
  output [15:0] CntOut,
  output [2:0] IndexOut
);

  wire comparator_1_eq, comparator_1_gt, or_1_out;

  Comparator #(.width(16), .mode("twosComplement")) comparator_1 (
    .a(Cnt1), .b(Cnt2), .gt(comparator_1_gt), .eq(comparator_1_eq));  // open: lt
  or or_1 (or_1_out, comparator_1_gt, comparator_1_eq);
  Multiplexer #(.select(1), .width(16), .disabled("Z"), .enable("false")) multiplexer_1 (
    .in0(Cnt1), .in1(Cnt2), .out(CntOut), .sel(or_1_out));
  Multiplexer #(.select(1), .width(3), .disabled("Z"), .enable("false")) multiplexer_2 (
    .in0(Index2), .in1(Index1), .out(IndexOut), .sel(or_1_out));
endmodule
